// Logisim project Guia_0401.circ as structural Verilog: 5 circuits, main circuit 01a
module _01a (
  input  x,
  input  y,
  input  z,
  output s_x_prime__y_prime_z_prime__prime
);

  wire not_1_out, not_2_out, or_1_out, w1_x_prime_out, w2_y_prime_out;

  not w1_x_prime (w1_x_prime_out, x);
  not w2_y_prime (w2_y_prime_out, y);
  not not_1 (not_1_out, z);
  or or_1 (or_1_out, w2_y_prime_out, not_1_out);
  not not_2 (not_2_out, or_1_out);
  and and_1 (s_x_prime__y_prime_z_prime__prime, w1_x_prime_out, not_2_out);

  // Notes on the sheet:
  //   w3=z'
  //   w4=w2+w3
  //   s=w1.w4
  //   w4'
endmodule

module _01b (
  input  x,
  input  y,
  input  z,
  output s__x_y__prime_z_prime
);

  wire not_1_out, not_2_out, or_1_out;

  not not_1 (not_1_out, z);
  or or_1 (or_1_out, x, y);
  not not_2 (not_2_out, or_1_out);
  and and_1 (s__x_y__prime_z_prime, not_2_out, not_1_out);

  // Notes on the sheet:
  //   w1=x+y
  //   w2=z'
  //   w3=w1'
  //   s=w3.w2
endmodule

module _01c (
  input  x,
  input  y,
  input  z,
  output s__x_y_prime__prime_z
);

  wire and_1_out, not_1_out, not_2_out;

  not not_1 (not_1_out, y);
  and and_1 (and_1_out, x, not_1_out);
  not not_2 (not_2_out, and_1_out);
  and and_2 (s__x_y_prime__prime_z, not_2_out, z);

  // Notes on the sheet:
  //   w1=y'
  //   w2=x.w1
  //   w3=w2'
  //   s=w3.z
endmodule

module _01d (
  input  x,
  input  y,
  input  z,
  output s__x_prime_y__prime_z
);

  wire and_1_out, not_1_out, not_2_out;

  not not_1 (not_1_out, x);
  and and_1 (and_1_out, not_1_out, y);
  not not_2 (not_2_out, and_1_out);
  and and_2 (s__x_prime_y__prime_z, not_2_out, z);

  // Notes on the sheet:
  //   w1=x'
  //   w2=y.w1
  //   w3=w2'
  //   s=w3.z
endmodule

module _01e (
  input  x,
  input  y,
  input  z,
  output s__x_y__prime__y_prime_z_prime
);

  wire not_1_out, not_2_out, or_1_out, or_2_out;

  not not_1 (not_1_out, y);
  not not_2 (not_2_out, z);
  or or_1 (or_1_out, x, not_1_out);
  or or_2 (or_2_out, not_1_out, not_2_out);
  and and_1 (s__x_y__prime__y_prime_z_prime, or_1_out, or_2_out);

  // Notes on the sheet:
  //   w1=y'
  //   w2=z'
  //   w3=x+w1
  //   w4=w1+w2
  //   s=w3.w4
endmodule
