// Logisim project Exemplo_0500.circ as structural Verilog: 1 circuit, main circuit main
module main (
  input  a,
  input  b,
  output s__w1_b_a_prime_b
);

  wire not_1_out;

  not not_1 (not_1_out, a);
  and and_1 (s__w1_b_a_prime_b, not_1_out, b);

  // Notes on the sheet:
  //   w1=a'
endmodule
