// Logisim project Exemplo_0501.circ as structural Verilog: 1 circuit, main circuit main
module main (
  input  a,
  input  b,
  output s__w1_w2_a_prime_b_prime,
  output out_4
);

  wire nand_1_out, nand_2_out, nand_3_out, not_1_out, not_2_out;

  not not_1 (not_1_out, a);
  not not_2 (not_2_out, b);
  and and_1 (s__w1_w2_a_prime_b_prime, not_1_out, not_2_out);
  nand nand_1 (nand_1_out, a, a);
  nand nand_2 (nand_2_out, nand_1_out, nand_3_out);
  nand nand_3 (nand_3_out, b, b);
  nand nand_4 (out_4, nand_2_out, nand_2_out);

  // Notes on the sheet:
  //   w1=a'
  //   w2=b'
  //   w1=nand(a,a)=a'
  //   w2=nand(b,b)=b'
  //   w3=nand(w1,w2)
  //   s =nand(w3,w3)=a'.b'
endmodule
