// Logisim project Exemplo_0502.circ as structural Verilog: 1 circuit, main circuit main
module main (
  input  a,
  input  b,
  output s__w1_b_a_prime_b,
  output out_4
);

  wire nor_1_out, nor_2_out, not_1_out;

  not not_1 (not_1_out, a);
  or or_1 (s__w1_b_a_prime_b, not_1_out, b);
  nor nor_1 (nor_1_out, a, a);
  nor nor_2 (nor_2_out, nor_1_out, b);
  nor nor_3 (out_4, nor_2_out, nor_2_out);

  // Notes on the sheet:
  //   w1=a'
  //   w1=nor(a,a)=a'
  //   w2=nor(w1,b) = a.b'
  //   s =nor(w2,w2)=a'+b
endmodule
