// Logisim project Exemplo_0503.circ as structural Verilog: 1 circuit, main circuit main
module main (
  input  a,
  input  b,
  output s__w1_a_a_b_prime,
  output out_4
);

  wire nand_1_out, not_1_out;

  not not_1 (not_1_out, b);
  or or_1 (s__w1_a_a_b_prime, a, not_1_out);
  nand nand_1 (nand_1_out, a, a);
  nand nand_2 (out_4, nand_1_out, b);

  // Notes on the sheet:
  //   w1=b'
  //   w2=nand(a,a)=a'
  //   s =nand(w2,a)=a+b'
endmodule
