// Logisim project Exemplo_0504.circ as structural Verilog: 1 circuit, main circuit main
module main (
  input  a,
  input  b,
  output s__w1_b_a_prime_b,
  output out_4
);

  wire nor_2_out, not_1_out;

  not not_1 (not_1_out, a);
  and and_1 (s__w1_b_a_prime_b, not_1_out, b);
  nor nor_1 (out_4, a, nor_2_out);
  nor nor_2 (nor_2_out, b, b);

  // Notes on the sheet:
  //   w1=a'
  //   w2=nor(b,b)=b'
  //   s =nor(a,w2)=a'.b
endmodule
