// Logisim project Exemplo_0505.circ as structural Verilog: 1 circuit, main circuit main
module main (
  input  a,
  input  b,
  output out_3,
  output out_4
);

  wire nand_1_out, nand_2_out, nand_3_out, nand_4_out, nand_5_out;

  xnor xnor_1 (out_3, a, b);
  nand nand_1 (nand_1_out, a, a);
  nand nand_2 (nand_2_out, b, b);
  nand nand_3 (nand_3_out, nand_1_out, b);
  nand nand_4 (nand_4_out, nand_3_out, nand_5_out);
  nand nand_5 (nand_5_out, nand_2_out, a);
  nand nand_6 (out_4, nand_4_out, nand_4_out);

  // Notes on the sheet:
  //   w1=nand(nand(a,a),b)=(~(~a.b))
  //   w2=nand(a,nand(b,b))=(~(a.~b))
  //   s=xnor(a,b) = (~(a^b))
  //   =(~(~a.b)).(~(a.~b)) = (~(a^b))
  //   s=xnor(a,b) = nand(nand(w1,w2),nand(w1,w2))
endmodule
