// Logisim project Exemplo_0506.circ as structural Verilog: 1 circuit, main circuit main
module main (
  input  a,
  input  b,
  output out_3,
  output out_4
);

  wire nor_1_out, nor_2_out, nor_3_out, nor_4_out, nor_5_out;

  xor xor_1 (out_3, a, b);
  nor nor_1 (nor_1_out, a, a);
  nor nor_2 (nor_2_out, b, b);
  nor nor_3 (nor_3_out, nor_1_out, b);
  nor nor_4 (nor_4_out, nor_3_out, nor_5_out);
  nor nor_5 (nor_5_out, nor_2_out, a);
  nor nor_6 (out_4, nor_4_out, nor_4_out);

  // Notes on the sheet:
  //   w1=nor(nor(a,a),b)=(~a.b)
  //   w2=nor(a,nor(b,b))=(a.~b)
  //   s=xor(a,b) = (a'.b)+(a.b')=(a^b)
  //   =(~a.b).(a.~b) = (a^b)
  //   s=nor(a,b) = nor(nor(w1,w2),nor(w1,w2))
endmodule
