// Logisim project Exemplo_0507.circ as structural Verilog: 1 circuit, main circuit main
module main (
  input  a,
  input  b,
  output out_3,
  output out_4
);

  wire nand_1_out, nand_2_out, nand_3_out, nand_4_out, nand_5_out, not_1_out, not_2_out, xor_1_out;

  not not_1 (not_1_out, a);
  not not_2 (not_2_out, b);
  nand nand_1 (nand_1_out, a, a);
  nand nand_2 (nand_2_out, b, b);
  not not_3 (out_3, xor_1_out);
  xor xor_1 (xor_1_out, not_1_out, not_2_out);
  nand nand_3 (nand_3_out, nand_1_out, b);
  nand nand_4 (nand_4_out, nand_3_out, nand_5_out);
  nand nand_5 (nand_5_out, nand_2_out, a);
  nand nand_6 (out_4, nand_4_out, nand_4_out);

  // Notes on the sheet:
  //   w1=a'
  //   w2=b'
  //   w3=w1^w2
  //   w4=nand(nand(a,a),b)=(~(~a.b))
  //   w5=nand(a,nand(b,b))=(~(a.~b))
  //   s=w3'=(xor(a',b'))' = (~(~a^~b))
  //   =(~(a.~b)).(~(~a.b)) = (~(~a^~b))
  //   s=xnor(a,b) = nand(nand(w4,w5),nand(w4,w5))
endmodule
