// Logisim project Exemplo_0508.circ as structural Verilog: 1 circuit, main circuit main
module main (
  input  a,
  input  b,
  output out_3,
  output s__w3__a_prime_b__prime
);

  wire and_1_out, nor_1_out, nor_2_out, not_1_out;

  not not_1 (not_1_out, a);
  and and_1 (and_1_out, not_1_out, b);
  nor nor_1 (nor_1_out, a, nor_2_out);
  nor nor_2 (nor_2_out, b, b);
  not not_2 (out_3, and_1_out);
  nor nor_3 (s__w3__a_prime_b__prime, nor_1_out, nor_1_out);

  // Notes on the sheet:
  //   w1=a'
  //   w2=nor(b,b)=b'
  //   w3=nor(w2,w2)=not(w2)
  //   s =(w1.b)'=(a'.b)'
endmodule
