// Logisim project Guia_0601.circ as structural Verilog: 5 circuits, main circuit 01.a
module _01_a (
  input  x,
  input  y,
  input  z,
  output s_w1_w2_w3,
  output s_w4_w5
);

  wire and_1_out, and_2_out, and_3_out, and_4_out, and_5_out, not_1_out, not_2_out, not_3_out, not_4_out;

  not not_1 (not_1_out, x);
  not not_2 (not_2_out, y);
  not not_3 (not_3_out, x);
  not not_4 (not_4_out, x);
  and and_1 (and_1_out, not_1_out, not_2_out, z);
  and and_2 (and_2_out, not_3_out, y, z);
  and and_3 (and_3_out, x, y, z);
  and and_4 (and_4_out, not_4_out, z);
  and and_5 (and_5_out, y, z);
  or or_1 (s_w1_w2_w3, and_1_out, and_2_out, and_3_out);
  or or_2 (s_w4_w5, and_4_out, and_5_out);

  // Notes on the sheet:
  //   m(1,3,7) = x'.y'.z + x'.y.z + x.y.z
  //   w1=x'.y'.z
  //   w2=x'.y.z
  //   w3=x.y.z
  //   w4=x'.z
  //   w5=y.z
endmodule

module _01_b (
  input  x,
  input  y,
  input  z,
  output s_w1_w2_w3,
  output s_w4_w5
);

  wire and_1_out, and_2_out, and_3_out, and_4_out, and_5_out, not_1_out, not_2_out, not_3_out, not_4_out,
       not_5_out, not_6_out, not_7_out;

  not not_1 (not_1_out, x);
  not not_2 (not_2_out, z);
  not not_3 (not_3_out, y);
  not not_4 (not_4_out, z);
  not not_5 (not_5_out, z);
  not not_6 (not_6_out, z);
  not not_7 (not_7_out, z);
  and and_1 (and_1_out, not_1_out, y, not_2_out);
  and and_2 (and_2_out, x, not_3_out, not_4_out);
  and and_3 (and_3_out, x, y, not_5_out);
  and and_4 (and_4_out, x, not_6_out);
  and and_5 (and_5_out, y, not_7_out);
  or or_1 (s_w1_w2_w3, and_1_out, and_2_out, and_3_out);
  or or_2 (s_w4_w5, and_4_out, and_5_out);

  // Notes on the sheet:
  //   m(2,4,6) = x'.y.z' + x.y'.z' + x.y.z'
  //   w1=x'.y.z'
  //   w2=x.y'.z'
  //   w3=x.y.z'
  //   w4=x.z'
  //   w5=y.z'
endmodule

module _01_c (
  input  x,
  input  y,
  input  z,
  output out_4,
  output s_w5_w6_w7
);

  wire and_1_out, and_2_out, and_3_out, and_4_out, and_5_out, and_6_out, and_7_out, not_1_out, not_2_out,
       not_3_out, not_4_out, not_5_out, not_6_out, not_7_out, not_8_out;

  not not_1 (not_1_out, x);
  not not_2 (not_2_out, z);
  not not_3 (not_3_out, y);
  not not_4 (not_4_out, z);
  not not_5 (not_5_out, y);
  not not_6 (not_6_out, y);
  not not_7 (not_7_out, x);
  not not_8 (not_8_out, z);
  and and_1 (and_1_out, not_1_out, y, not_2_out);
  and and_2 (and_2_out, x, not_3_out, not_4_out);
  and and_3 (and_3_out, x, not_5_out, z);
  and and_4 (and_4_out, x, y, z);
  and and_5 (and_5_out, x, not_6_out);
  and and_6 (and_6_out, x, z);
  and and_7 (and_7_out, not_7_out, y, not_8_out);
  or or_1 (out_4, and_1_out, and_2_out, and_3_out, and_4_out);
  or or_2 (s_w5_w6_w7, and_5_out, and_6_out, and_7_out);

  // Notes on the sheet:
  //   w1=x'.y.z'
  //   w2=x.y'.z'
  //   w3=x.y'.z
  //   w4=x.y.z
  //   w5=x.y'
  //   w6=x.z
  //   w7=x'.y.z'
  //   m(2,4,5,7) = x'.y.z' + x.y'.z' + x.y'.z + x.y.z
  //   s=w1+w2+w3+w4
endmodule

module _01_d (
  input  x,
  input  y,
  input  z,
  output out_4,
  output s_w5_w6_w7
);

  wire and_1_out, and_2_out, and_3_out, and_4_out, and_5_out, and_6_out, and_7_out, not_1_out, not_2_out,
       not_3_out, not_4_out, not_5_out, not_6_out, not_7_out;

  not not_1 (not_1_out, x);
  not not_2 (not_2_out, y);
  not not_3 (not_3_out, x);
  not not_4 (not_4_out, z);
  not not_5 (not_5_out, x);
  not not_6 (not_6_out, x);
  not not_7 (not_7_out, x);
  and and_1 (and_1_out, not_1_out, not_2_out, z);
  and and_2 (and_2_out, not_3_out, y, not_4_out);
  and and_3 (and_3_out, not_5_out, y, z);
  and and_4 (and_4_out, x, y, z);
  and and_5 (and_5_out, not_6_out, z);
  and and_6 (and_6_out, not_7_out, y);
  and and_7 (and_7_out, y, z);
  or or_1 (out_4, and_1_out, and_2_out, and_3_out, and_4_out);
  or or_2 (s_w5_w6_w7, and_5_out, and_6_out, and_7_out);

  // Notes on the sheet:
  //   w1=x'.y'.z
  //   w2=x'.y.z'
  //   w3=x.y.z'
  //   w4=x.y.z
  //   w5=x'.z
  //   w6=x.'y
  //   w7=y.z
  //   m(1,2,3,7) = x'.y'.z + x'.y.z' + x'.y.z + x.y.z
  //   s=w1+w2+w3+w4
endmodule

module _01_e (
  input  x,
  input  y,
  input  z,
  output out_4,
  output s_w5_w6
);

  wire and_1_out, and_2_out, and_3_out, and_4_out, and_5_out, and_6_out, not_1_out, not_2_out, not_3_out,
       not_4_out, not_5_out, not_6_out, not_7_out, not_8_out;

  not not_1 (not_1_out, x);
  not not_2 (not_2_out, y);
  not not_3 (not_3_out, z);
  not not_4 (not_4_out, x);
  not not_5 (not_5_out, z);
  not not_6 (not_6_out, z);
  not not_7 (not_7_out, x);
  not not_8 (not_8_out, z);
  and and_1 (and_1_out, not_1_out, not_2_out, not_3_out);
  and and_2 (and_2_out, not_4_out, y, not_5_out);
  and and_3 (and_3_out, x, y, not_6_out);
  and and_4 (and_4_out, x, y, z);
  and and_5 (and_5_out, not_7_out, not_8_out);
  and and_6 (and_6_out, x, y);
  or or_1 (out_4, and_1_out, and_2_out, and_3_out, and_4_out);
  or or_2 (s_w5_w6, and_5_out, and_6_out);

  // Notes on the sheet:
  //   w1=x'.y'.z'
  //   w2=x'.y.z'
  //   w3=x.y.z'
  //   w4=x.y.z
  //   w5=x'.z'
  //   w6=x.y
  //   m(0,2,6,7) = x'.y'.z' + x'.y.z' + x.y.z' + x.y.z
  //   s=w1+w2+w3+w4
endmodule
