// Logisim project Guia_0602.circ as structural Verilog: 5 circuits, main circuit 02.a
module _02_a (
  input  X,
  input  Y,
  input  Z,
  output S_W1_W2_W3,
  output S_W4_W5
);

  wire not_1_out, not_2_out, not_3_out, not_4_out, not_5_out, not_6_out, not_7_out, not_8_out, not_9_out,
       or_1_out, or_2_out, or_3_out, or_4_out, or_5_out;

  not not_1 (not_1_out, X);
  not not_2 (not_2_out, X);
  not not_3 (not_3_out, Z);
  not not_4 (not_4_out, X);
  not not_5 (not_5_out, Y);
  not not_6 (not_6_out, Z);
  not not_7 (not_7_out, X);
  not not_8 (not_8_out, X);
  not not_9 (not_9_out, Z);
  or or_1 (or_1_out, not_1_out, Y, Z);
  or or_2 (or_2_out, not_2_out, Y, not_3_out);
  or or_3 (or_3_out, not_4_out, not_5_out, not_6_out);
  or or_4 (or_4_out, not_7_out, Y);
  or or_5 (or_5_out, not_8_out, not_9_out);
  and and_1 (S_W1_W2_W3, or_1_out, or_2_out, or_3_out);
  and and_2 (S_W4_W5, or_4_out, or_5_out);

  // Notes on the sheet:
  //   W1=X'+Y+Z
  //   W2=X'+Y+Z'
  //   W3=X'+Y'+Z'
  //   W4=X'+Y
  //   W5=X'+Z'
  //   M(4,5,7) = X'+Y+Z . X'+Y+Z' . X'+Y'+Z'
endmodule

module _02_b (
  input  X,
  input  Y,
  input  Z,
  output S_W1_W2_W3,
  output S_W4_W5
);

  wire not_1_out, not_2_out, not_3_out, not_4_out, not_5_out, not_6_out, not_7_out, not_8_out, not_9_out,
       or_1_out, or_2_out, or_3_out, or_4_out, or_5_out;

  not not_1 (not_1_out, Z);
  not not_2 (not_2_out, X);
  not not_3 (not_3_out, Y);
  not not_4 (not_4_out, X);
  not not_5 (not_5_out, Y);
  not not_6 (not_6_out, Z);
  not not_7 (not_7_out, X);
  not not_8 (not_8_out, Y);
  not not_9 (not_9_out, Z);
  or or_1 (or_1_out, X, Y, not_1_out);
  or or_2 (or_2_out, not_2_out, not_3_out, Z);
  or or_3 (or_3_out, not_4_out, not_5_out, not_6_out);
  or or_4 (or_4_out, not_7_out, not_8_out);
  or or_5 (or_5_out, X, Y, not_9_out);
  and and_1 (S_W1_W2_W3, or_1_out, or_2_out, or_3_out);
  and and_2 (S_W4_W5, or_4_out, or_5_out);

  // Notes on the sheet:
  //   W1=X+Y+Z'
  //   W2=X'+Y+Z'
  //   W3=X'+Y'+Z'
  //   W4=X'+Y'
  //   W5=X+Y+Z'
  //   M(1,6,7) = X+Y+Z' . X'+Y'+Z . X'+Y'+Z'
endmodule

module _02_c (
  input  X,
  input  Y,
  input  Z,
  output out_4,
  output out_5
);

  wire not_1_out, not_2_out, not_3_out, not_4_out, not_5_out, not_6_out, not_7_out, not_8_out, or_1_out,
       or_2_out, or_3_out, or_4_out, or_5_out, or_6_out;

  not not_1 (not_1_out, Z);
  not not_2 (not_2_out, Y);
  not not_3 (not_3_out, Y);
  not not_4 (not_4_out, Z);
  not not_5 (not_5_out, X);
  not not_6 (not_6_out, Y);
  not not_7 (not_7_out, Z);
  not not_8 (not_8_out, Y);
  or or_1 (or_1_out, X, Y, not_1_out);
  or or_2 (or_2_out, X, not_2_out, Z);
  or or_3 (or_3_out, X, not_3_out, not_4_out);
  or or_4 (or_4_out, not_5_out, not_6_out, Z);
  or or_5 (or_5_out, X, not_7_out);
  or or_6 (or_6_out, not_8_out, Z);
  and and_1 (out_4, or_1_out, or_2_out, or_3_out, or_4_out);
  and and_2 (out_5, or_5_out, or_6_out);

  // Notes on the sheet:
  //   W1=X+Y+Z'
  //   W2=X+Y'+Z
  //   W3=X+Y'+Z'
  //   W4=X'+Y'+Z
  //   W5=X+Z'
  //   W6=Y'+Z
  //   M(1,2,3,6) = X+Y+Z' . X+Y'+Z . X+Y'+Z' . X'+Y'+Z
  //   S=W1+W2+W3+W4
  //   S=W5+W6
endmodule

module _02_d (
  input  X,
  input  Y,
  input  Z,
  output out_4,
  output S_W5_W6_W7
);

  wire not_1_out, not_2_out, not_3_out, not_4_out, not_5_out, not_6_out, not_7_out, not_8_out, not_9_out,
       not_10_out, not_11_out, or_1_out, or_2_out, or_3_out, or_4_out, or_5_out, or_6_out, or_7_out;

  not not_1 (not_1_out, Y);
  not not_2 (not_2_out, Z);
  not not_3 (not_3_out, X);
  not not_4 (not_4_out, Z);
  not not_5 (not_5_out, X);
  not not_6 (not_6_out, Y);
  not not_7 (not_7_out, Z);
  not not_8 (not_8_out, X);
  not not_9 (not_9_out, Z);
  not not_10 (not_10_out, Y);
  not not_11 (not_11_out, Z);
  or or_1 (or_1_out, X, Y, Z);
  or or_2 (or_2_out, X, not_1_out, not_2_out);
  or or_3 (or_3_out, not_3_out, Y, not_4_out);
  or or_4 (or_4_out, not_5_out, not_6_out, not_7_out);
  or or_5 (or_5_out, not_8_out, not_9_out);
  or or_6 (or_6_out, not_10_out, not_11_out);
  or or_7 (or_7_out, X, Y, Z);
  and and_1 (out_4, or_1_out, or_2_out, or_3_out, or_4_out);
  and and_2 (S_W5_W6_W7, or_5_out, or_6_out, or_7_out);

  // Notes on the sheet:
  //   W1=X+Y+Z
  //   W2=X+Y'+Z'
  //   W3=X'+Y+Z'
  //   W4=X'+Y'+Z'
  //   W5=X'+Z'
  //   W6=Y'+Z'
  //   W7=X+Y+Z
  //   M (0,3,5,7) = X+Y+Z . X+Y'+Z' . X'+Y+Z' . X'+Y'+Z'
  //   S=W1+W2+W3+W4
endmodule

module _02_e (
  input  X,
  input  Y,
  input  Z,
  output out_4,
  output out_5
);

  wire not_1_out, not_2_out, not_3_out, not_4_out, not_5_out, not_6_out, not_7_out, not_8_out, not_9_out,
       not_10_out, not_11_out, or_1_out, or_2_out, or_3_out, or_4_out, or_5_out, or_6_out;

  not not_1 (not_1_out, Z);
  not not_2 (not_2_out, Y);
  not not_3 (not_3_out, Z);
  not not_4 (not_4_out, X);
  not not_5 (not_5_out, Y);
  not not_6 (not_6_out, X);
  not not_7 (not_7_out, Y);
  not not_8 (not_8_out, Z);
  not not_9 (not_9_out, Z);
  not not_10 (not_10_out, X);
  not not_11 (not_11_out, Y);
  or or_1 (or_1_out, X, Y, not_1_out);
  or or_2 (or_2_out, X, not_2_out, not_3_out);
  or or_3 (or_3_out, not_4_out, not_5_out, Z);
  or or_4 (or_4_out, not_6_out, not_7_out, not_8_out);
  or or_5 (or_5_out, X, not_9_out);
  or or_6 (or_6_out, not_10_out, not_11_out);
  and and_1 (out_4, or_1_out, or_2_out, or_3_out, or_4_out);
  and and_2 (out_5, or_5_out, or_6_out);

  // Notes on the sheet:
  //   W1=X+Y+Z'
  //   W2=X+Y'+Z'
  //   W3=X+Y'+Z'
  //   W4=X'+Y'+Z
  //   W5=X+Z'
  //   W6=X'+Y'
  //   M(1,3,6,7) = X+Y+Z' . X+Y'+Z' . X'+Y'+Z . X'+Y'+Z'
  //   S=W1+W2+W3+W4
  //   S=W5+W6
endmodule
