// Logisim project Guia_0603.circ as structural Verilog: 2 circuits, main circuit 03.a
module _03_a (
  input  x,
  input  y,
  input  w,
  input  z,
  output out_5,
  output out_6
);

  wire and_1_out, and_2_out, and_3_out, and_4_out, and_5_out, and_6_out, and_7_out, and_8_out, and_9_out,
       not_1_out, not_2_out, not_3_out, not_4_out, not_5_out, not_6_out, not_7_out, not_8_out, not_9_out,
       not_10_out, not_11_out, not_12_out, not_13_out, not_14_out, not_15_out, not_16_out, not_17_out,
       not_18_out;

  not not_1 (not_1_out, y);
  not not_2 (not_2_out, y);
  not not_3 (not_3_out, z);
  not not_4 (not_4_out, y);
  not not_5 (not_5_out, x);
  not not_6 (not_6_out, w);
  not not_7 (not_7_out, x);
  not not_8 (not_8_out, y);
  not not_9 (not_9_out, w);
  not not_10 (not_10_out, x);
  not not_11 (not_11_out, y);
  not not_12 (not_12_out, z);
  not not_13 (not_13_out, x);
  not not_14 (not_14_out, w);
  not not_15 (not_15_out, y);
  not not_16 (not_16_out, w);
  not not_17 (not_17_out, y);
  not not_18 (not_18_out, z);
  and and_1 (and_1_out, not_7_out, not_8_out, not_9_out, z);
  and and_2 (and_2_out, not_10_out, not_11_out, w, not_12_out);
  and and_3 (and_3_out, not_13_out, y, not_14_out, z);
  and and_4 (and_4_out, x, not_15_out, not_16_out, z);
  and and_5 (and_5_out, x, not_17_out, w, not_18_out);
  and and_6 (and_6_out, x, not_1_out, w, z);
  and and_7 (and_7_out, not_2_out, w, not_3_out);
  and and_8 (and_8_out, x, not_4_out, z);
  and and_9 (and_9_out, not_5_out, not_6_out, z);
  or or_1 (out_5, and_1_out, and_2_out, and_3_out, and_4_out, and_5_out, and_6_out);
  or or_2 (out_6, and_7_out, and_8_out, and_9_out);

  // Notes on the sheet:
  //   f1=y'.w.z'
  //   f2=x.y'.z
  //   f3=x'.w'.z
  //   ( 1): x'.y'.w'.z
  //   ( 2): x'.y'.w .z'
  //   ( 5): x'.y .w'.z
  //   ( 9): x .y'.w'.z
  //   (10): x .y'.w.z'
  //   (11): x .y'.w .z
  //   SoP(1,2,5,9,10,11)
  //   s=f1+f2+f3
endmodule

module _03_b (
  input  x,
  input  y,
  input  w,
  input  z,
  output out_5,
  output out_6
);

  wire and_1_out, and_2_out, and_3_out, and_4_out, and_5_out, and_6_out, and_7_out, and_8_out, and_9_out,
       and_10_out, not_1_out, not_2_out, not_3_out, not_4_out, not_5_out, not_6_out, not_7_out, not_8_out,
       not_9_out, not_10_out, not_11_out, not_12_out, not_13_out, not_14_out, not_15_out, not_16_out,
       not_17_out, not_18_out, not_19_out, not_20_out, not_21_out, not_22_out, not_23_out;

  or or_1 (out_5, and_1_out, and_2_out, and_3_out);
  and and_1 (and_1_out, not_1_out, z);
  and and_2 (and_2_out, not_2_out, not_3_out, not_4_out);
  and and_3 (and_3_out, not_5_out, not_6_out, z);
  not not_1 (not_1_out, w);
  not not_2 (not_2_out, y);
  not not_3 (not_3_out, w);
  not not_4 (not_4_out, z);
  not not_5 (not_5_out, x);
  not not_6 (not_6_out, y);
  not not_7 (not_7_out, x);
  not not_8 (not_8_out, y);
  not not_9 (not_9_out, w);
  not not_10 (not_10_out, z);
  not not_11 (not_11_out, x);
  not not_12 (not_12_out, y);
  not not_13 (not_13_out, w);
  not not_14 (not_14_out, x);
  not not_15 (not_15_out, y);
  not not_16 (not_16_out, x);
  not not_17 (not_17_out, w);
  not not_18 (not_18_out, y);
  not not_19 (not_19_out, w);
  not not_20 (not_20_out, z);
  not not_21 (not_21_out, y);
  not not_22 (not_22_out, w);
  not not_23 (not_23_out, w);
  and and_4 (and_4_out, not_7_out, not_8_out, not_9_out, not_10_out);
  and and_5 (and_5_out, not_11_out, not_12_out, not_13_out, z);
  and and_6 (and_6_out, not_14_out, not_15_out, w, z);
  and and_7 (and_7_out, not_16_out, y, not_17_out, z);
  and and_8 (and_8_out, x, not_18_out, not_19_out, not_20_out);
  and and_9 (and_9_out, x, not_21_out, not_22_out, z);
  and and_10 (and_10_out, x, y, not_23_out, z);
  or or_2 (out_6, and_4_out, and_5_out, and_6_out, and_7_out, and_8_out, and_9_out, and_10_out);

  // Notes on the sheet:
  //   SoP(1,2,5,9,10,11)
  //   f1=w'.z
  //   f2=y'.w'.z'
  //   f3=x'.y'.z
  //   ( 0): x'.y'.w'.z'
  //   ( 1): x'.y'.w'.z
  //   ( 3): x'.y'.w .z
  //   ( 5): x'.y .w'.z
  //   ( 8): x. y'.w'.z'
  //   ( 9): x .y'.w'.z
  //   (13): x .y .w'.z
endmodule
