// Logisim project Exemplo_07.circ as structural Verilog: 16 circuits, main circuit 0702a
module _0701a (
  input  x,
  input  y,
  input  c,
  output s
);

  wire and_1_out, and_2_out, and_3_out, nand_1_out, not_1_out;

  and and_1 (and_1_out, y, x);
  nand nand_1 (nand_1_out, y, x);
  not not_1 (not_1_out, c);
  and and_2 (and_2_out, not_1_out, and_1_out);
  and and_3 (and_3_out, nand_1_out, c);
  or or_1 (s, and_2_out, and_3_out);

  // Notes on the sheet:
  //   s1 = AND
  //   s2 = NAND
  //   0
  //   1
endmodule

module _0701b (
  input  x,
  input  y,
  input  c,
  output s
);

  wire and_1_out, nand_1_out;

  and and_1 (and_1_out, y, x);
  nand nand_1 (nand_1_out, y, x);
  Multiplexer #(.enable("false")) multiplexer_1 (.in0(and_1_out), .in1(nand_1_out), .out(s), .sel(c));

  // Notes on the sheet:
  //   s1 = AND
  //   s2 = NAND
endmodule

module _0702a (
  input  x,
  input  y,
  input  c,
  output s
);

  wire and_1_out, and_2_out, nor_1_out, not_1_out, or_1_out;

  or or_1 (or_1_out, y, x);
  nor nor_1 (nor_1_out, y, x);
  not not_1 (not_1_out, c);
  and and_1 (and_1_out, not_1_out, or_1_out);
  and and_2 (and_2_out, nor_1_out, c);
  or or_2 (s, and_1_out, and_2_out);

  // Notes on the sheet:
  //   s1 = OR
  //   s2 = NOR
  //   0
  //   1
endmodule

module _0702b (
  input  x,
  input  y,
  input  c,
  output s
);

  wire nor_1_out, or_1_out;

  or or_1 (or_1_out, y, x);
  nor nor_1 (nor_1_out, y, x);
  Multiplexer #(.enable("false")) multiplexer_1 (.in0(or_1_out), .in1(nor_1_out), .out(s), .sel(c));

  // Notes on the sheet:
  //   s1 = OR
  //   s2 = NOR
endmodule

module _0703a (
  input  x,
  input  y,
  input  c1,
  input  c2,
  output s
);

  wire and_1_out, and_2_out, and_3_out, and_4_out, and_5_out, and_6_out, and_7_out, nand_1_out, nor_1_out,
       not_1_out, not_2_out, not_3_out, or_1_out, or_2_out, or_3_out;

  and and_1 (and_1_out, y, x);
  nand nand_1 (nand_1_out, y, x);
  or or_1 (or_1_out, y, x);
  nor nor_1 (nor_1_out, y, x);
  not not_1 (not_1_out, c1);
  and and_2 (and_2_out, not_1_out, and_1_out);
  and and_3 (and_3_out, nand_1_out, c1);
  not not_2 (not_2_out, c1);
  and and_4 (and_4_out, not_2_out, or_1_out);
  and and_5 (and_5_out, nor_1_out, c1);
  or or_2 (or_2_out, and_2_out, and_3_out);
  or or_3 (or_3_out, and_4_out, and_5_out);
  not not_3 (not_3_out, c2);
  and and_6 (and_6_out, not_3_out, or_2_out);
  and and_7 (and_7_out, c2, or_3_out);
  or or_4 (s, and_6_out, and_7_out);

  // Notes on the sheet:
  //   s1 = AND
  //   s2 = NAND
  //   s3 = OR
  //   s4 = NOR
  //   0
  //   1
  //   0
  //   1
  //   s12
  //   s34
  //   0
  //   1
endmodule

module _0703b (
  input  x,
  input  y,
  input  c1,
  input  c2,
  output s
);

  wire and_1_out, multiplexer_1_out, multiplexer_2_out, nand_1_out, nor_1_out, or_1_out;

  and and_1 (and_1_out, y, x);
  nand nand_1 (nand_1_out, y, x);
  or or_1 (or_1_out, y, x);
  nor nor_1 (nor_1_out, y, x);
  Multiplexer #(.enable("false")) multiplexer_1 (.in0(and_1_out), .in1(nand_1_out), .out(multiplexer_1_out), .sel(c1));
  Multiplexer #(.enable("false")) multiplexer_2 (.in0(or_1_out), .in1(nor_1_out), .out(multiplexer_2_out), .sel(c1));
  Multiplexer #(.enable("false")) multiplexer_3 (.in0(multiplexer_1_out), .in1(multiplexer_2_out), .out(s), .sel(c2));

  // Notes on the sheet:
  //   s1 = AND
  //   s2 = NAND
  //   s3 = OR
  //   s4 = NOR
  //   s12
  //   s34
endmodule

module _0704a (
  input  x,
  input  y,
  input  c1,
  input  c2,
  output s
);

  wire and_1_out, and_2_out, and_3_out, and_4_out, nor_1_out, not_1_out, not_2_out, or_1_out, xnor_1_out,
       xor_1_out;

  xor xor_1 (xor_1_out, y, x);
  xnor xnor_1 (xnor_1_out, y, x);
  or or_1 (or_1_out, y, x);
  nor nor_1 (nor_1_out, y, x);
  not not_1 (not_1_out, c2);
  not not_2 (not_2_out, c1);
  and and_1 (and_1_out, not_1_out, not_2_out, xor_1_out);
  and and_2 (and_2_out, c1, not_1_out, xnor_1_out);
  and and_3 (and_3_out, not_2_out, c2, or_1_out);
  and and_4 (and_4_out, c1, c2, nor_1_out);
  or or_2 (s, and_1_out, and_2_out, and_3_out, and_4_out);

  // Notes on the sheet:
  //   s1 = XOR
  //   s2 = OR
  //   s3 = XNOR
  //   s4 = NOR
endmodule

module _0704b (
  input  x,
  input  y,
  input  [1:0] c1c2,
  output s
);

  wire nor_1_out, or_1_out, xnor_1_out, xor_1_out;

  xor xor_1 (xor_1_out, y, x);
  xnor xnor_1 (xnor_1_out, y, x);
  or or_1 (or_1_out, y, x);
  nor nor_1 (nor_1_out, y, x);
  Multiplexer #(.select(2), .enable("false")) multiplexer_1 (
    .in0(xor_1_out), .in1(xnor_1_out), .in2(or_1_out), .in3(nor_1_out), .out(s), .sel(c1c2));

  // Notes on the sheet:
  //   s1 = XOR
  //   s2 = XNOR
  //   s3 = OR
  //   s4 = NOR
endmodule

module _0705a (
  input  x,
  input  y,
  input  c1,
  input  c2,
  input  c3,
  output s
);

  wire and_1_out, and_2_out, and_3_out, and_4_out, and_5_out, and_6_out, and_7_out, and_8_out, and_9_out,
       nand_1_out, nor_1_out, not_1_out, not_2_out, not_3_out, not_4_out, not_5_out, or_1_out, xnor_1_out,
       xor_1_out;

  not not_1 (not_1_out, x);
  and and_1 (and_1_out, y, x);
  nand nand_1 (nand_1_out, y, x);
  xor xor_1 (xor_1_out, y, x);
  xnor xnor_1 (xnor_1_out, y, x);
  or or_1 (or_1_out, y, x);
  nor nor_1 (nor_1_out, y, x);
  not not_2 (not_2_out, y);
  not not_3 (not_3_out, c2);
  not not_4 (not_4_out, c1);
  not not_5 (not_5_out, c3);
  and and_2 (and_2_out, not_4_out, not_3_out, not_5_out, not_1_out);
  and and_3 (and_3_out, c1, not_3_out, not_5_out, and_1_out);
  and and_4 (and_4_out, not_4_out, c2, not_5_out, nand_1_out);
  and and_5 (and_5_out, c1, c2, not_5_out, xor_1_out);
  and and_6 (and_6_out, not_4_out, not_3_out, c3, xnor_1_out);
  and and_7 (and_7_out, c1, not_3_out, c3, or_1_out);
  and and_8 (and_8_out, not_4_out, c2, c3, nor_1_out);
  and and_9 (and_9_out, c1, c2, c3, not_2_out);
  or or_2 (s, and_2_out, and_3_out, and_4_out, and_5_out, and_6_out, and_7_out, and_8_out, and_9_out);

  // Notes on the sheet:
  //   s1 = NOT(x)
  //   s2 = AND
  //   s3 = NAND
  //   s4 = XOR
  //   s5 = XNOR
  //   s6 = OR
  //   s7 = NOR
  //   s8 = NOT(y)
endmodule

module _0705b (
  input  x,
  input  y,
  input  [2:0] c1c2c3,
  output s
);

  wire and_1_out, nand_1_out, nor_1_out, not_1_out, not_2_out, or_1_out, xnor_1_out, xor_1_out;

  not not_1 (not_1_out, x);
  and and_1 (and_1_out, y, x);
  nand nand_1 (nand_1_out, y, x);
  xor xor_1 (xor_1_out, y, x);
  xnor xnor_1 (xnor_1_out, y, x);
  or or_1 (or_1_out, y, x);
  nor nor_1 (nor_1_out, y, x);
  not not_2 (not_2_out, y);
  Multiplexer #(.select(3), .enable("false")) multiplexer_1 (
    .in0(not_1_out), .in1(and_1_out), .in2(nand_1_out), .in3(xor_1_out), .in4(xnor_1_out), .in5(or_1_out),
    .in6(nor_1_out), .in7(not_2_out), .out(s), .sel(c1c2c3));

  // Notes on the sheet:
  //   s1 = NOT(x)
  //   s2 = AND
  //   s3 = NAND
  //   s4 = XOR
  //   s5 = XNOR
  //   s6 = OR
  //   s7 = NOR
  //   s8 = NOT(y)
endmodule

module _0706 (
  input  [1:0] x,
  input  [1:0] y,
  input  c,
  output out_4
);

  wire isdiferent_1_isdiferent_x_y, isequals_1_isequals_x_y;

  isEquals isequals_1 (.x(x), .y(y), .isEquals_x_y(isequals_1_isequals_x_y));
  isDiferent isdiferent_1 (.x(x), .y(y), .isDiferent_x_y(isdiferent_1_isdiferent_x_y));
  Multiplexer #(.enable("false")) multiplexer_1 (
    .in0(isequals_1_isequals_x_y), .in1(isdiferent_1_isdiferent_x_y), .out(out_4), .sel(c));

  // Notes on the sheet:
  //   =
  //   !=
  //   isEquals(x,y)
  //   isDiferent(x,y)
endmodule

module _0707 (
  input  [1:0] x,
  input  [1:0] y,
  input  c,
  output out_4
);

  wire islessthan_1_islessthan_x_y, ismorethan_1_ismorethan_x_y;

  isLessThan islessthan_1 (.x(x), .y(y), .isLessThan_x_y(islessthan_1_islessthan_x_y));
  isMoreThan ismorethan_1 (.x(x), .y(y), .isMoreThan_x_y(ismorethan_1_ismorethan_x_y));
  Multiplexer #(.enable("false")) multiplexer_1 (
    .in0(islessthan_1_islessthan_x_y), .in1(ismorethan_1_ismorethan_x_y), .out(out_4), .sel(c));

  // Notes on the sheet:
  //   <
  //   >
  //   isLessThan(x,y)
  //   isMoreThan(x,y)
endmodule

module isEquals (
  input  [1:0] x,
  input  [1:0] y,
  output isEquals_x_y
);

  wire xnor_1_out, xnor_2_out;

  xnor xnor_1 (xnor_1_out, x[1], y[1]);
  xnor xnor_2 (xnor_2_out, x[0], y[0]);
  and and_1 (isEquals_x_y, xnor_1_out, xnor_2_out);

  // Notes on the sheet:
  //   isEquals(x[1],y[1])
  //   isEquals(x[0],y[0])
endmodule

module isDiferent (
  input  [1:0] x,
  input  [1:0] y,
  output isDiferent_x_y
);

  wire xor_1_out, xor_2_out;

  xor xor_1 (xor_1_out, x[1], y[1]);
  xor xor_2 (xor_2_out, x[0], y[0]);
  or or_1 (isDiferent_x_y, xor_1_out, xor_2_out);

  // Notes on the sheet:
  //   isDiferent(x[1],y[1])
  //   isDiferent(x[0],y[0])
endmodule

module isLessThan (
  input  [1:0] x,
  input  [1:0] y,
  output isLessThan_x_y
);

  wire and_1_out, and_2_out, and_3_out, not_1_out, not_2_out, not_3_out, not_4_out;

  not not_1 (not_1_out, x[1]);
  and and_1 (and_1_out, not_1_out, y[1]);
  not not_2 (not_2_out, x[0]);
  and and_2 (and_2_out, not_2_out, y[1], y[0]);
  not not_3 (not_3_out, x[1]);
  and and_3 (and_3_out, not_3_out, not_4_out, y[0]);
  not not_4 (not_4_out, x[0]);
  or or_1 (isLessThan_x_y, and_1_out, and_2_out, and_3_out);

  // Notes on the sheet:
  //   a
  //   b
  //   w1=a'.c
  //   w2=b'.c.d
  //   w3=a'.b'.d
  //   c
  //   d
endmodule

module isMoreThan (
  input  [1:0] x,
  input  [1:0] y,
  output isMoreThan_x_y
);

  wire and_1_out, and_2_out, and_3_out, not_1_out, not_2_out, not_3_out, not_4_out;

  and and_1 (and_1_out, x[1], not_1_out);
  not not_1 (not_1_out, y[1]);
  and and_2 (and_2_out, x[0], not_2_out, not_3_out);
  not not_2 (not_2_out, y[1]);
  not not_3 (not_3_out, y[0]);
  and and_3 (and_3_out, x[1], x[0], not_4_out);
  not not_4 (not_4_out, y[0]);
  or or_1 (isMoreThan_x_y, and_1_out, and_2_out, and_3_out);

  // Notes on the sheet:
  //   b
  //   a
  //   w1=a.c'
  //   w2=b.c'.d'
  //   w3=a.b.d'
  //   c
  //   d
endmodule
