// Logisim project Exemplo_08.circ as structural Verilog
module _0801 (
  input  [4:0] a_4_0,
  input  [4:0] b_4_0,
  output s0_5,
  output s0_4,
  output s0_3,
  output s0_2,
  output s0_1,
  output s0_0
);

  wire fulladder_1_s1, fulladder_2_s1, fulladder_3_s1, fulladder_4_s1;

  fullAdder fulladder_1 (.CarryIn(1'b0), .x(a_4_0[0]), .y(b_4_0[0]), .s1(fulladder_1_s1), .s0(s0_0));
  fullAdder fulladder_2 (.CarryIn(fulladder_1_s1), .x(a_4_0[1]), .y(b_4_0[1]), .s1(fulladder_2_s1), .s0(s0_1));
  fullAdder fulladder_3 (.CarryIn(fulladder_2_s1), .x(a_4_0[2]), .y(b_4_0[2]), .s1(fulladder_3_s1), .s0(s0_2));
  fullAdder fulladder_4 (.CarryIn(fulladder_3_s1), .x(a_4_0[3]), .y(b_4_0[3]), .s1(fulladder_4_s1), .s0(s0_3));
  fullAdder fulladder_5 (.CarryIn(fulladder_4_s1), .x(a_4_0[4]), .y(b_4_0[4]), .s1(s0_5), .s0(s0_4));
endmodule

module _0802 (
  input  [4:0] a_4_0,
  input  [4:0] b_4_0,
  output s0_5,
  output s0_4,
  output s0_3,
  output s0_2,
  output s0_1,
  output s0_0
);

  wire fulldifference_1_s1, fulldifference_2_s1, fulldifference_3_s1, fulldifference_4_s1;

  fullDifference fulldifference_1 (.CarryIn(1'b0), .x(a_4_0[0]), .y(b_4_0[0]), .s1(fulldifference_1_s1), .s0(s0_0));
  fullDifference fulldifference_2 (
    .CarryIn(fulldifference_1_s1), .x(a_4_0[1]), .y(b_4_0[1]), .s1(fulldifference_2_s1), .s0(s0_1));
  fullDifference fulldifference_3 (
    .CarryIn(fulldifference_2_s1), .x(a_4_0[2]), .y(b_4_0[2]), .s1(fulldifference_3_s1), .s0(s0_2));
  fullDifference fulldifference_4 (
    .CarryIn(fulldifference_3_s1), .x(a_4_0[3]), .y(b_4_0[3]), .s1(fulldifference_4_s1), .s0(s0_3));
  fullDifference fulldifference_5 (.CarryIn(fulldifference_4_s1), .x(a_4_0[4]), .y(b_4_0[4]), .s1(s0_5), .s0(s0_4));
endmodule

module _0803 (
  input  [4:0] a_4_0,
  input  [4:0] b_4_0,
  output isEquals
);

  wire isequals_1_s, isequals_2_s, isequals_3_s, isequals_4_s;

  isEquals isequals_1 (.CarryIn(1'b1), .x(a_4_0[0]), .y(b_4_0[0]), .s(isequals_1_s));
  isEquals isequals_2 (.CarryIn(isequals_1_s), .x(a_4_0[1]), .y(b_4_0[1]), .s(isequals_2_s));
  isEquals isequals_3 (.CarryIn(isequals_2_s), .x(a_4_0[2]), .y(b_4_0[2]), .s(isequals_3_s));
  isEquals isequals_4 (.CarryIn(isequals_3_s), .x(a_4_0[3]), .y(b_4_0[3]), .s(isequals_4_s));
  isEquals isequals_5 (.CarryIn(isequals_4_s), .x(a_4_0[4]), .y(b_4_0[4]), .s(isEquals));
endmodule

module _0804 (
  input  [4:0] a_4_0,
  input  [4:0] b_4_0,
  output isDifferent
);

  wire isdifferent_1_s, isdifferent_2_s, isdifferent_3_s, isdifferent_4_s;

  isDifferent isdifferent_1 (.CarryIn(1'b0), .x(a_4_0[0]), .y(b_4_0[0]), .s(isdifferent_1_s));
  isDifferent isdifferent_2 (.CarryIn(isdifferent_1_s), .x(a_4_0[1]), .y(b_4_0[1]), .s(isdifferent_2_s));
  isDifferent isdifferent_3 (.CarryIn(isdifferent_2_s), .x(a_4_0[2]), .y(b_4_0[2]), .s(isdifferent_3_s));
  isDifferent isdifferent_4 (.CarryIn(isdifferent_3_s), .x(a_4_0[3]), .y(b_4_0[3]), .s(isdifferent_4_s));
  isDifferent isdifferent_5 (.CarryIn(isdifferent_4_s), .x(a_4_0[4]), .y(b_4_0[4]), .s(isDifferent));
endmodule

module _0805 (
  input  [4:0] x,
  output sinal,
  output out_3,
  output a_4_0,
  output out_5,
  output out_6,
  output out_7
);

  Complement2 complement2_1 (
    .a_4_0(x), .s0_5(sinal), .s0_4(out_3), .s0_3(a_4_0), .s0_2(out_5), .s0_1(out_6), .s0_0(out_7));
endmodule

module halfAdder (
  input  x,
  input  y,
  output s1,
  output s0
);

  and and_1 (s1, x, y);
  xor xor_1 (s0, y, x);
endmodule

module fullAdder (
  input  x,
  input  y,
  input  CarryIn,
  output s0,
  output s1
);

  wire halfadder_1_s0, halfadder_1_s1, halfadder_2_s1;

  halfAdder halfadder_1 (.x(x), .y(y), .s1(halfadder_1_s1), .s0(halfadder_1_s0));
  halfAdder halfadder_2 (.x(halfadder_1_s0), .y(CarryIn), .s1(halfadder_2_s1), .s0(s0));
  or or_1 (s1, halfadder_1_s1, halfadder_2_s1);
endmodule

module halfDifference (
  input  x,
  input  y,
  output s1,
  output s0
);

  wire not_1_out;

  not not_1 (not_1_out, x);
  and and_1 (s1, not_1_out, y);
  xor xor_1 (s0, y, x);
endmodule

module fullDifference (
  input  x,
  input  y,
  input  CarryIn,
  output s0,
  output s1
);

  wire halfdifference_1_s0, halfdifference_1_s1, halfdifference_2_s1;

  halfDifference halfdifference_1 (.x(x), .y(y), .s1(halfdifference_1_s1), .s0(halfdifference_1_s0));
  halfDifference halfdifference_2 (.x(halfdifference_1_s0), .y(CarryIn), .s1(halfdifference_2_s1), .s0(s0));
  or or_1 (s1, halfdifference_1_s1, halfdifference_2_s1);
endmodule

module isEquals (
  input  x,
  input  y,
  input  CarryIn,
  output s
);

  wire xnor_1_out;

  xnor xnor_1 (xnor_1_out, x, y);
  and and_1 (s, CarryIn, xnor_1_out);
endmodule

module isDifferent (
  input  x,
  input  y,
  input  CarryIn,
  output s
);

  wire xor_1_out;

  xor xor_1 (xor_1_out, x, y);
  or or_1 (s, CarryIn, xor_1_out);
endmodule

module Complement1 (
  input  [4:0] x,
  output s_5,
  output s_4,
  output s_3,
  output s_2,
  output s_1,
  output s_0
);

  not not_1 (s_4, x[4]);
  not not_2 (s_2, x[2]);
  not not_3 (s_0, x[0]);
  not not_4 (s_1, x[1]);
  not not_5 (s_3, x[3]);

  assign s_5 = 1'b1;
endmodule

module Complement2 (
  input  [4:0] a_4_0,
  output s0_5,
  output s0_4,
  output s0_3,
  output s0_2,
  output s0_1,
  output s0_0
);

  wire complement1_1_s_0, complement1_1_s_1, complement1_1_s_2, complement1_1_s_3, complement1_1_s_4,
       fulladder_1_s1, fulladder_2_s1, fulladder_3_s1, fulladder_4_s1;

  Complement1 complement1_1 (
    .x(a_4_0), .s_5(s0_5), .s_4(complement1_1_s_4), .s_3(complement1_1_s_3), .s_2(complement1_1_s_2),
    .s_1(complement1_1_s_1), .s_0(complement1_1_s_0));
  fullAdder fulladder_1 (.CarryIn(1'b0), .x(complement1_1_s_0), .y(1'b1), .s1(fulladder_1_s1), .s0(s0_0));
  fullAdder fulladder_2 (.CarryIn(fulladder_1_s1), .x(complement1_1_s_1), .y(1'b0), .s1(fulladder_2_s1), .s0(s0_1));
  fullAdder fulladder_3 (.CarryIn(fulladder_2_s1), .x(complement1_1_s_2), .y(1'b0), .s1(fulladder_3_s1), .s0(s0_2));
  fullAdder fulladder_4 (.CarryIn(fulladder_3_s1), .x(complement1_1_s_3), .y(1'b0), .s1(fulladder_4_s1), .s0(s0_3));
  // fullAdder fulladder_5: pin names not known; wires that end beside it: fulladder_4_s1, complement1_1_s_4, 1'b0, 1'b0, s0_4

  // Notes on the sheet:
  //   // desconsiderar o "vai um"
  //   sinal
endmodule
