// Logisim project Exemplo_11.circ as structural Verilog: 16 circuits, main circuit Moore_1101.v
// Mealy
module Mealy_1101_v (
  input  clk,
  input  x,
  input  reset,
  output y
);

  wire d_ff_1_q, d_ff_2_q, d_ff_2_qn, d_ff_3_q, d_ff_4_q;

  D_Flip_Flop d_ff_1 (.clk(clk), .D(x), .Q(d_ff_1_q), .reset(reset));  // open: Qn, preset
  D_Flip_Flop d_ff_2 (.clk(clk), .D(d_ff_1_q), .Q(d_ff_2_q), .Qn(d_ff_2_qn), .reset(reset));  // open: preset
  D_Flip_Flop d_ff_3 (.clk(clk), .D(d_ff_2_q), .Q(d_ff_3_q), .reset(reset));  // open: Qn, preset
  D_Flip_Flop d_ff_4 (.clk(clk), .D(d_ff_3_q), .Q(d_ff_4_q), .reset(reset));  // open: Qn, preset
  and and_1 (y, d_ff_4_q, d_ff_3_q, d_ff_2_qn, d_ff_1_q);

  // Notes on the sheet:
  //   module mealy_1101 (y, x, clk, reset)
  //   1 _ _ _
  //   _ 1 _ _
  //   _ _ 0 _
  //   _ _ _ 1
endmodule

// Moore
module Moore_1101_v (
  input  clk,
  input  x,
  input  reset,
  output y
);

  wire and_1_out, d_ff_1_q, d_ff_2_q, d_ff_2_qn, d_ff_3_q, d_ff_4_q;

  D_Flip_Flop d_ff_1 (.clk(clk), .D(x), .Q(d_ff_1_q), .reset(reset));  // open: Qn, preset
  D_Flip_Flop d_ff_2 (.clk(clk), .D(d_ff_1_q), .Q(d_ff_2_q), .Qn(d_ff_2_qn), .reset(reset));  // open: preset
  D_Flip_Flop d_ff_3 (.clk(clk), .D(d_ff_2_q), .Q(d_ff_3_q), .reset(reset));  // open: Qn, preset
  D_Flip_Flop d_ff_4 (.clk(clk), .D(d_ff_3_q), .Q(d_ff_4_q), .reset(reset));  // open: Qn, preset
  and and_1 (and_1_out, d_ff_4_q, d_ff_3_q, d_ff_2_qn, d_ff_1_q);
  D_Flip_Flop d_ff_5 (.clk(clk), .D(and_1_out), .Q(y), .reset(reset));  // open: Qn, preset

  // Notes on the sheet:
  //   module moore_1101 (y, x, clk, reset)
  //   1 _ _ _
  //   _ 1 _ _
  //   _ _ 0 _
  //   _ _ _ 1
  //   1 1 0 1
endmodule

module Exemplo_1101_v (
  input  x,
  input  reset,
  output Mealy_s1__x__clk__reset,
  output Moore_s1__x__clk__reset
);

  wire clk_out;

  Mealy_1101_v mealy_1101_v_1 (.clk(clk_out), .x(x), .reset(reset), .y(Mealy_s1__x__clk__reset));
  Moore_1101_v moore_1101_v_1 (.clk(clk_out), .x(x), .reset(reset), .y(Moore_s1__x__clk__reset));
  Clock clk (.out(clk_out));
endmodule

module Exemplo_1102_v (
  input  x,
  input  reset,
  output Mealy_s1__x__clk__reset,
  output Moore_s1__x__clk__reset
);

  wire clk_out;

  Mealy_1101_v mealy_1101_v_1 (.clk(clk_out), .x(x), .reset(reset), .y(Mealy_s1__x__clk__reset));
  Moore_1101_v moore_1101_v_1 (.clk(clk_out), .x(x), .reset(reset), .y(Moore_s1__x__clk__reset));
  Clock clk (.out(clk_out));
endmodule

// Mealy
module Mealy_1011_semIntersecao_v (
  input  clk,
  input  x,
  input  reset,
  output y
);

  wire d_ff_1_q, d_ff_2_q, d_ff_3_q, d_ff_3_qn, d_ff_4_q, d_ff_5_q, or_1_out;

  D_Flip_Flop d_ff_1 (.clk(clk), .D(x), .Q(d_ff_1_q), .reset(reset));  // open: Qn, preset
  D_Flip_Flop d_ff_2 (.clk(clk), .D(d_ff_1_q), .Q(d_ff_2_q), .reset(or_1_out));  // open: Qn, preset
  or or_1 (or_1_out, reset, d_ff_5_q);
  D_Flip_Flop d_ff_3 (.clk(clk), .D(d_ff_2_q), .Q(d_ff_3_q), .Qn(d_ff_3_qn), .reset(or_1_out));  // open: preset
  D_Flip_Flop d_ff_4 (.clk(clk), .D(d_ff_3_q), .Q(d_ff_4_q), .reset(or_1_out));  // open: Qn, preset
  and and_1 (y, d_ff_4_q, d_ff_3_qn, d_ff_2_q, d_ff_1_q);
  D_Flip_Flop d_ff_5 (.clk(clk), .D(y), .Q(d_ff_5_q), .reset(or_1_out));  // open: Qn, preset

  // Notes on the sheet:
  //   module mealy_1011_semIntersecao (y, x, clk, reset)
  //   1 _ _ _
  //   _ 0 _ _
  //   _ _ 1 _
  //   _ _ _ 1
endmodule

module Mealy_1011_comIntersecao_v (
  input  clk,
  input  x,
  input  reset,
  output y
);

  wire d_ff_1_q, d_ff_2_q, d_ff_3_q, d_ff_3_qn, d_ff_4_q;

  D_Flip_Flop d_ff_1 (.clk(clk), .D(x), .Q(d_ff_1_q), .reset(reset));  // open: Qn, preset
  D_Flip_Flop d_ff_2 (.clk(clk), .D(d_ff_1_q), .Q(d_ff_2_q), .reset(reset));  // open: Qn, preset
  D_Flip_Flop d_ff_3 (.clk(clk), .D(d_ff_2_q), .Q(d_ff_3_q), .Qn(d_ff_3_qn), .reset(reset));  // open: preset
  D_Flip_Flop d_ff_4 (.clk(clk), .D(d_ff_3_q), .Q(d_ff_4_q), .reset(reset));  // open: Qn, preset
  and and_1 (y, d_ff_4_q, d_ff_3_qn, d_ff_2_q, d_ff_1_q);

  // Notes on the sheet:
  //   module mealy_1011_comIntersecao (y, x, clk, reset)
  //   1 _ _ _
  //   _ 0 _ _
  //   _ _ 1 _
  //   _ _ _ 1
endmodule

module Exemplo_1103_v (
  input  x,
  input  reset,
  output Mealy_1011_semIntersecao_s1__x__clk__reset
);

  wire clk_out;

  Clock clk (.out(clk_out));
  Mealy_1011_semIntersecao_v mealy_1011_semintersecao_v_1 (
    .clk(clk_out), .x(x), .reset(reset), .y(Mealy_1011_semIntersecao_s1__x__clk__reset));
endmodule

module Moore_1011_semIntercesao_v (
  input  clk,
  input  x,
  input  reset,
  output y
);

  wire and_1_out, d_ff_1_q, d_ff_2_q, d_ff_3_q, d_ff_3_qn, d_ff_4_q, d_ff_6_q, or_1_out;

  D_Flip_Flop d_ff_1 (.clk(clk), .D(x), .Q(d_ff_1_q), .reset(reset));  // open: Qn, preset
  D_Flip_Flop d_ff_2 (.clk(clk), .D(d_ff_1_q), .Q(d_ff_2_q), .reset(or_1_out));  // open: Qn, preset
  or or_1 (or_1_out, reset, d_ff_6_q);
  D_Flip_Flop d_ff_3 (.clk(clk), .D(d_ff_2_q), .Q(d_ff_3_q), .Qn(d_ff_3_qn), .reset(or_1_out));  // open: preset
  D_Flip_Flop d_ff_4 (.clk(clk), .D(d_ff_3_q), .Q(d_ff_4_q), .reset(or_1_out));  // open: Qn, preset
  and and_1 (and_1_out, d_ff_4_q, d_ff_3_qn, d_ff_2_q, d_ff_1_q);
  D_Flip_Flop d_ff_5 (.clk(clk), .D(and_1_out), .Q(y), .reset(reset));  // open: Qn, preset
  D_Flip_Flop d_ff_6 (.clk(clk), .D(and_1_out), .Q(d_ff_6_q), .reset(or_1_out));  // open: Qn, preset

  // Notes on the sheet:
  //   module moore_1011_semIntersecao (y, x, clk, reset)
  //   1 _ _ _
  //   _ 0 _ _
  //   _ _ 1 _
  //   _ _ _ 1
  //   1 0 1 1
endmodule

// Moore
module Moore_1011_comIntersecao_v (
  input  clk,
  input  x,
  input  reset,
  output y
);

  wire and_1_out, d_ff_1_q, d_ff_2_q, d_ff_3_q, d_ff_3_qn, d_ff_4_q;

  D_Flip_Flop d_ff_1 (.clk(clk), .D(x), .Q(d_ff_1_q), .reset(reset));  // open: Qn, preset
  D_Flip_Flop d_ff_2 (.clk(clk), .D(d_ff_1_q), .Q(d_ff_2_q), .reset(reset));  // open: Qn, preset
  D_Flip_Flop d_ff_3 (.clk(clk), .D(d_ff_2_q), .Q(d_ff_3_q), .Qn(d_ff_3_qn), .reset(reset));  // open: preset
  D_Flip_Flop d_ff_4 (.clk(clk), .D(d_ff_3_q), .Q(d_ff_4_q), .reset(reset));  // open: Qn, preset
  and and_1 (and_1_out, d_ff_4_q, d_ff_3_qn, d_ff_2_q, d_ff_1_q);
  D_Flip_Flop d_ff_5 (.clk(clk), .D(and_1_out), .Q(y), .reset(reset));  // open: Qn, preset

  // Notes on the sheet:
  //   module moore_1011_comIntersecao (y, x, clk, reset)
  //   1 _ _ _
  //   _ 0 _ _
  //   _ _ 1 _
  //   _ _ _ 1
  //   1 1 0 1
endmodule

module Exemplo_1104_v (
  input  x,
  input  reset,
  output Moore_1011_comIntersecao_s1__x__clk__reset
);

  wire clk_out;

  Clock clk (.out(clk_out));
  Moore_1011_comIntersecao_v moore_1011_comintersecao_v_1 (
    .clk(clk_out), .x(x), .reset(reset), .y(Moore_1011_comIntersecao_s1__x__clk__reset));
endmodule

// Mealy
module Mealy_x000_v (
  input  clk,
  input  x,
  output y
);

  wire d_ff_1_q, d_ff_1_qn, d_ff_2_q, d_ff_2_qn, d_ff_3_q, d_ff_3_qn, d_ff_4_q, d_ff_4_qn, or_1_out, undriven;

  D_Flip_Flop d_ff_1 (.clk(clk), .D(x), .Q(d_ff_1_q), .Qn(d_ff_1_qn), .preset(undriven), .reset(undriven));
  D_Flip_Flop d_ff_2 (.clk(clk), .D(d_ff_1_q), .Q(d_ff_2_q), .Qn(d_ff_2_qn));  // open: preset, reset
  D_Flip_Flop d_ff_3 (.clk(clk), .D(d_ff_2_q), .Q(d_ff_3_q), .Qn(d_ff_3_qn));  // open: preset, reset
  D_Flip_Flop d_ff_4 (.clk(clk), .D(d_ff_3_q), .Q(d_ff_4_q), .Qn(d_ff_4_qn));  // open: preset, reset
  or or_1 (or_1_out, d_ff_4_q, d_ff_4_qn);
  and and_1 (y, or_1_out, d_ff_3_qn, d_ff_2_qn, d_ff_1_qn);

  // Notes on the sheet:
  //   module mealy_x000 (y, x, clk)
  //   x _ _ _
  //   _ 0 _ _
  //   _ _ 0 _
  //   _ _ _ 0
endmodule

// Moore
module Moore_x000_v (
  input  clk,
  input  x,
  input  reset,
  output y
);

  wire and_1_out, d_ff_1_q, d_ff_1_qn, d_ff_2_q, d_ff_2_qn, d_ff_3_q, d_ff_3_qn, d_ff_4_q, d_ff_4_qn,
       or_1_out;

  D_Flip_Flop d_ff_1 (.clk(clk), .D(x), .Q(d_ff_1_q), .Qn(d_ff_1_qn), .reset(reset));  // open: preset
  D_Flip_Flop d_ff_2 (.clk(clk), .D(d_ff_1_q), .Q(d_ff_2_q), .Qn(d_ff_2_qn), .reset(reset));  // open: preset
  D_Flip_Flop d_ff_3 (.clk(clk), .D(d_ff_2_q), .Q(d_ff_3_q), .Qn(d_ff_3_qn), .reset(reset));  // open: preset
  D_Flip_Flop d_ff_4 (.clk(clk), .D(d_ff_3_q), .Q(d_ff_4_q), .Qn(d_ff_4_qn), .reset(reset));  // open: preset
  or or_1 (or_1_out, d_ff_4_q, d_ff_4_qn);
  and and_1 (and_1_out, or_1_out, d_ff_3_qn, d_ff_2_qn, d_ff_1_qn);
  D_Flip_Flop d_ff_5 (.clk(clk), .D(and_1_out), .Q(y), .reset(reset));  // open: Qn, preset

  // Notes on the sheet:
  //   module moore_1101 (y, x, clk, reset)
  //   x _ _ _
  //   _ 0 _ _
  //   _ _ 0 _
  //   _ _ _ 0
  //   x 0 0 0
endmodule

module Exemplo_1105_v (
  input  x,
  input  reset,
  output Mealy_x000_s1__x__clk,
  output Moore_x000_s1__x__clk__reset
);

  wire clk_out;

  Mealy_x000_v mealy_x000_v_1 (.clk(clk_out), .x(x), .y(Mealy_x000_s1__x__clk));
  Moore_x000_v moore_x000_v_1 (.clk(clk_out), .x(x), .reset(reset), .y(Moore_x000_s1__x__clk__reset));
  Clock clk (.out(clk_out));
endmodule

// Mealy
module Mealy_010_or_101_v (
  input  clk,
  input  x,
  input  reset,
  output y
);

  wire and_1_out, and_2_out, d_ff_1_q, d_ff_1_qn, d_ff_2_q, d_ff_2_qn, d_ff_3_q, d_ff_3_qn;

  D_Flip_Flop d_ff_1 (.clk(clk), .D(x), .Q(d_ff_1_q), .Qn(d_ff_1_qn), .reset(reset));  // open: preset
  D_Flip_Flop d_ff_2 (.clk(clk), .D(d_ff_1_q), .Q(d_ff_2_q), .Qn(d_ff_2_qn), .reset(reset));  // open: preset
  D_Flip_Flop d_ff_3 (.clk(clk), .D(d_ff_2_q), .Q(d_ff_3_q), .Qn(d_ff_3_qn), .reset(reset));  // open: preset
  and and_1 (and_1_out, d_ff_3_q, d_ff_2_qn, d_ff_1_q);
  or or_1 (y, and_1_out, and_2_out);
  and and_2 (and_2_out, d_ff_3_qn, d_ff_2_q, d_ff_1_qn);

  // Notes on the sheet:
  //   module mealy_101_or_010 (y, x, clk, reset)
  //   1 0 1
  //    0 1 0
endmodule

// Moore
module Moore_010_or_101_v (
  input  clk,
  input  x,
  input  reset,
  output y
);

  wire and_1_out, and_2_out, d_ff_1_q, d_ff_1_qn, d_ff_2_q, d_ff_2_qn, d_ff_3_q, d_ff_3_qn, or_1_out;

  D_Flip_Flop d_ff_1 (.clk(clk), .D(x), .Q(d_ff_1_q), .Qn(d_ff_1_qn), .reset(reset));  // open: preset
  D_Flip_Flop d_ff_2 (.clk(clk), .D(d_ff_1_q), .Q(d_ff_2_q), .Qn(d_ff_2_qn), .reset(reset));  // open: preset
  D_Flip_Flop d_ff_3 (.clk(clk), .D(d_ff_2_q), .Q(d_ff_3_q), .Qn(d_ff_3_qn), .reset(reset));  // open: preset
  and and_1 (and_1_out, d_ff_3_q, d_ff_2_qn, d_ff_1_q);
  and and_2 (and_2_out, d_ff_3_qn, d_ff_2_q, d_ff_1_qn);
  or or_1 (or_1_out, and_1_out, and_2_out);
  D_Flip_Flop d_ff_4 (.clk(clk), .D(or_1_out), .Q(y), .reset(reset));  // open: Qn, preset

  // Notes on the sheet:
  //   module moore_101_or_010 (y, x, clk, reset)
  //   1 0  1 _
  //   0 1 0 _
  //   1 0 1 || 0 1 0
endmodule

module Exemplo_1106_v (
  input  x,
  input  reset,
  output Mealy_010_or_101__s1__x__clk__reset,
  output Moore_010_or_101__s1__x__clk__reset
);

  wire clk_out;

  Mealy_010_or_101_v mealy_010_or_101_v_1 (
    .clk(clk_out), .x(x), .reset(reset), .y(Mealy_010_or_101__s1__x__clk__reset));
  Moore_010_or_101_v moore_010_or_101_v_1 (
    .clk(clk_out), .x(x), .reset(reset), .y(Moore_010_or_101__s1__x__clk__reset));
  Clock clk (.out(clk_out));
endmodule
