// Logisim project Exemplo_12.circ as structural Verilog
module RAM_1x2 (
  input  CLK,
  input  [1:0] \input ,
  input  R_W,
  input  ADDR,
  input  CLR,
  output [1:0] \output 
);

  wire and_1_out, j_k_ff_1_q, j_k_ff_2_q, not_1_out;

  and and_1 (and_1_out, CLK, R_W, ADDR);
  not not_1 (not_1_out, R_W);
  J_K_Flip_Flop j_k_ff_1 (
    .J(\input [1]), .clk(and_1_out), .K(\input [1]), .Q(j_k_ff_1_q), .reset(CLR));  // open: Qn, preset
  J_K_Flip_Flop j_k_ff_2 (
    .J(\input [0]), .clk(and_1_out), .K(\input [0]), .Q(j_k_ff_2_q), .reset(CLR));  // open: Qn, preset
  and and_2 (\output [0], j_k_ff_2_q, not_1_out, ADDR);
  and and_3 (\output [1], j_k_ff_1_q, not_1_out, ADDR);
endmodule

module RAM_1x4 (
  input  CLK,
  input  [3:0] \input ,
  input  R_W,
  input  ADDR,
  input  CLR,
  output [3:0] \output 
);

  wire and_1_out, j_k_ff_1_q, j_k_ff_2_q, j_k_ff_3_q, j_k_ff_4_q, not_1_out;

  not not_1 (not_1_out, R_W);
  and and_1 (and_1_out, CLK, R_W, ADDR);
  J_K_Flip_Flop j_k_ff_1 (
    .J(\input [3]), .clk(and_1_out), .K(\input [3]), .Q(j_k_ff_1_q), .reset(CLR));  // open: Qn, preset
  J_K_Flip_Flop j_k_ff_2 (
    .J(\input [2]), .clk(and_1_out), .K(\input [2]), .Q(j_k_ff_2_q), .reset(CLR));  // open: Qn, preset
  J_K_Flip_Flop j_k_ff_3 (
    .J(\input [1]), .clk(and_1_out), .K(\input [1]), .Q(j_k_ff_3_q), .reset(CLR));  // open: Qn, preset
  J_K_Flip_Flop j_k_ff_4 (
    .J(\input [0]), .clk(and_1_out), .K(\input [0]), .Q(j_k_ff_4_q), .reset(CLR));  // open: Qn, preset
  and and_2 (\output [0], j_k_ff_4_q, not_1_out, ADDR);
  and and_3 (\output [1], j_k_ff_3_q, not_1_out, ADDR);
  and and_4 (\output [2], j_k_ff_2_q, not_1_out, ADDR);
  and and_5 (\output [3], j_k_ff_1_q, not_1_out, ADDR);
endmodule

module RAM_2x4 (
  input  [3:0] \input ,
  input  CLK,
  input  R_W,
  input  ADDR,
  input  CLR,
  output [3:0] \output 
);

  wire and_1_out, and_2_out, j_k_ff_1_q, j_k_ff_2_q, j_k_ff_3_q, j_k_ff_4_q, j_k_ff_5_q, j_k_ff_6_q,
       j_k_ff_7_q, j_k_ff_8_q, not_1_out, not_2_out, not_3_out, not_4_out;
  wire [3:0] and_3_out, and_7_out;

  not not_1 (not_1_out, ADDR);
  not not_2 (not_2_out, R_W);
  not not_3 (not_3_out, not_1_out);
  and and_1 (and_1_out, CLK, R_W, ADDR);
  and and_2 (and_2_out, CLK, R_W, not_4_out);
  not not_4 (not_4_out, ADDR);
  J_K_Flip_Flop j_k_ff_1 (
    .J(\input [3]), .clk(and_1_out), .K(\input [3]), .Q(j_k_ff_1_q), .reset(CLR));  // open: Qn, preset
  J_K_Flip_Flop j_k_ff_2 (
    .J(\input [3]), .clk(and_2_out), .K(\input [3]), .Q(j_k_ff_2_q), .reset(CLR));  // open: Qn, preset
  J_K_Flip_Flop j_k_ff_3 (
    .J(\input [2]), .clk(and_1_out), .K(\input [2]), .Q(j_k_ff_3_q), .reset(CLR));  // open: Qn, preset
  J_K_Flip_Flop j_k_ff_4 (
    .J(\input [2]), .clk(and_2_out), .K(\input [2]), .Q(j_k_ff_4_q), .reset(CLR));  // open: Qn, preset
  J_K_Flip_Flop j_k_ff_5 (
    .J(\input [1]), .clk(and_1_out), .K(\input [1]), .Q(j_k_ff_5_q), .reset(CLR));  // open: Qn, preset
  J_K_Flip_Flop j_k_ff_6 (
    .J(\input [1]), .clk(and_2_out), .K(\input [1]), .Q(j_k_ff_6_q), .reset(CLR));  // open: Qn, preset
  J_K_Flip_Flop j_k_ff_7 (
    .J(\input [0]), .clk(and_1_out), .K(\input [0]), .Q(j_k_ff_7_q), .reset(CLR));  // open: Qn, preset
  J_K_Flip_Flop j_k_ff_8 (
    .J(\input [0]), .clk(and_2_out), .K(\input [0]), .Q(j_k_ff_8_q), .reset(CLR));  // open: Qn, preset
  and and_3 (and_3_out[0], j_k_ff_8_q, not_2_out, not_1_out);
  and and_4 (and_3_out[1], j_k_ff_6_q, not_2_out, not_1_out);
  and and_5 (and_3_out[2], j_k_ff_4_q, not_2_out, not_1_out);
  and and_6 (and_3_out[3], j_k_ff_2_q, not_2_out, not_1_out);
  and and_7 (and_7_out[0], j_k_ff_1_q, not_2_out, not_3_out);
  and and_8 (and_7_out[1], j_k_ff_3_q, not_2_out, not_3_out);
  and and_9 (and_7_out[2], j_k_ff_5_q, not_2_out, not_3_out);
  and and_10 (and_7_out[3], j_k_ff_7_q, not_2_out, not_3_out);
  Multiplexer #(.width(4), .enable("false")) multiplexer_1 (
    .in0(and_3_out), .in1(and_7_out), .out(\output ), .sel(ADDR));
endmodule

module RAM_1x4__2_1x2 (
  input  CLK,
  input  W_R,
  input  [3:0] \input ,
  input  ADDR,
  input  CLR,
  output [3:0] \output 
);

  RAM_1x2 ram_1x2_1 (.CLK(CLK), .R_W(W_R), .ADDR(ADDR), .CLR(CLR), .\input (\input [1:0]), .\output (\output [1:0]));
  RAM_1x2 ram_1x2_2 (.CLK(CLK), .R_W(W_R), .ADDR(ADDR), .CLR(CLR), .\input (\input [3:2]), .\output (\output [3:2]));
endmodule

module RAM_2x4__2_1x4 (
  input  CLK,
  input  W_R,
  input  [3:0] \input ,
  input  ADDR,
  input  CLR,
  output [3:0] \output 
);

  wire not_1_out;
  wire [3:0] ram_1x4_1_output, ram_1x4_2_output;

  RAM_1x4 ram_1x4_1 (.CLK(CLK), .R_W(W_R), .ADDR(not_1_out), .CLR(CLR), .\input (\input ), .\output (ram_1x4_1_output));
  not not_1 (not_1_out, ADDR);
  RAM_1x4 ram_1x4_2 (.CLK(CLK), .R_W(W_R), .ADDR(ADDR), .CLR(CLR), .\input (\input ), .\output (ram_1x4_2_output));
  Multiplexer #(.width(4), .enable("false")) multiplexer_1 (
    .in0(ram_1x4_1_output), .in1(ram_1x4_2_output), .out(\output ), .sel(ADDR));
endmodule

module RAM_4x8__4_2x4 (
  input  [7:0] \input ,
  input  CLK,
  input  W_R,
  input  [1:0] ADDR,
  input  CLR,
  output [7:0] \output 
);

  wire and_1_out, and_2_out, and_3_out, and_4_out, not_1_out, not_2_out;
  wire [3:0] ram_2x4_1_output, ram_2x4_2_output, ram_2x4_3_output, ram_2x4_4_output;

  not not_1 (not_1_out, ADDR[1]);
  and and_1 (and_1_out, not_1_out, CLK);
  not not_2 (not_2_out, ADDR[1]);
  and and_2 (and_2_out, not_2_out, W_R);
  and and_3 (and_3_out, ADDR[1], CLK);
  and and_4 (and_4_out, ADDR[1], W_R);
  RAM_2x4 ram_2x4_1 (
    .CLK(and_1_out), .R_W(and_2_out), .ADDR(ADDR[0]), .CLR(CLR), .\input (\input [3:0]),
    .\output (ram_2x4_1_output));
  RAM_2x4 ram_2x4_2 (
    .CLK(and_1_out), .R_W(and_2_out), .ADDR(ADDR[0]), .CLR(CLR), .\input (\input [7:4]),
    .\output (ram_2x4_2_output));
  RAM_2x4 ram_2x4_3 (
    .CLK(and_3_out), .R_W(and_4_out), .ADDR(ADDR[0]), .CLR(CLR), .\input (\input [3:0]),
    .\output (ram_2x4_3_output));
  RAM_2x4 ram_2x4_4 (
    .CLK(and_3_out), .R_W(and_4_out), .ADDR(ADDR[0]), .CLR(CLR), .\input (\input [7:4]),
    .\output (ram_2x4_4_output));
  Multiplexer #(.select(2), .width(4), .enable("false")) multiplexer_1 (
    .in0(ram_2x4_1_output), .in1(ram_2x4_1_output), .in2(ram_2x4_3_output), .in3(ram_2x4_3_output),
    .out(\output [3:0]), .sel(ADDR));
  Multiplexer #(.select(2), .width(4), .enable("false")) multiplexer_2 (
    .in0(ram_2x4_2_output), .in1(ram_2x4_2_output), .in2(ram_2x4_4_output), .in3(ram_2x4_4_output),
    .out(\output [7:4]), .sel(ADDR));
endmodule

module RAM_8x8__2_4x8 (
  input  CLK,
  input  [7:0] \input ,
  input  W_R,
  input  [2:0] ADDR,
  input  CLR,
  output [7:0] \output 
);

  wire and_1_out, and_2_out, and_3_out, and_4_out, not_1_out, not_2_out;
  wire [7:0] ram_4x8__4_2x4_1_output, ram_4x8__4_2x4_2_output;

  not not_1 (not_1_out, ADDR[2]);
  not not_2 (not_2_out, ADDR[2]);
  and and_1 (and_1_out, not_1_out, CLK);
  and and_2 (and_2_out, not_2_out, W_R);
  RAM_4x8__4_2x4 ram_4x8__4_2x4_1 (
    .CLK(and_1_out), .W_R(and_2_out), .ADDR(ADDR[1:0]), .CLR(CLR), .\input (\input ),
    .\output (ram_4x8__4_2x4_1_output));
  RAM_4x8__4_2x4 ram_4x8__4_2x4_2 (
    .CLK(and_3_out), .W_R(and_4_out), .ADDR(ADDR[1:0]), .CLR(CLR), .\input (\input ),
    .\output (ram_4x8__4_2x4_2_output));
  and and_3 (and_3_out, ADDR[2], CLK);
  and and_4 (and_4_out, ADDR[2], W_R);
  Multiplexer #(.width(8), .enable("false")) multiplexer_1 (
    .in0(ram_4x8__4_2x4_1_output), .in1(ram_4x8__4_2x4_2_output), .out(\output ), .sel(ADDR[2]));
endmodule

module RAM_4x16__2_4x8 (
  input  CLK,
  input  W_R,
  input  [15:0] \input ,
  input  [1:0] ADDR,
  input  CLR,
  output [15:0] \output 
);

  RAM_4x8__4_2x4 ram_4x8__4_2x4_1 (
    .CLK(CLK), .W_R(W_R), .ADDR(ADDR), .CLR(CLR), .\input (\input [7:0]), .\output (\output [7:0]));
  RAM_4x8__4_2x4 ram_4x8__4_2x4_2 (
    .CLK(CLK), .W_R(W_R), .ADDR(ADDR), .CLR(CLR), .\input (\input [15:8]), .\output (\output [15:8]));
endmodule

module RAM_1x16 (
  input  CLK,
  input  R_W,
  input  ADDR,
  input  [15:0] \input ,
  input  clr,
  output [15:0] \output 
);

  wire and_1_out, j_k_ff_1_q, j_k_ff_2_q, j_k_ff_3_q, j_k_ff_4_q, j_k_ff_5_q, j_k_ff_6_q, j_k_ff_7_q,
       j_k_ff_8_q, j_k_ff_9_q, j_k_ff_10_q, j_k_ff_11_q, j_k_ff_12_q, j_k_ff_13_q, j_k_ff_14_q, j_k_ff_15_q,
       j_k_ff_16_q, not_1_out;

  and and_1 (and_1_out, CLK, R_W, ADDR);
  not not_1 (not_1_out, R_W);
  J_K_Flip_Flop j_k_ff_1 (
    .J(\input [15]), .clk(and_1_out), .K(\input [15]), .Q(j_k_ff_1_q), .reset(clr));  // open: Qn, preset
  J_K_Flip_Flop j_k_ff_2 (
    .J(\input [7]), .clk(and_1_out), .K(\input [7]), .Q(j_k_ff_2_q), .reset(clr));  // open: Qn, preset
  J_K_Flip_Flop j_k_ff_3 (
    .J(\input [14]), .clk(and_1_out), .K(\input [14]), .Q(j_k_ff_3_q), .reset(clr));  // open: Qn, preset
  J_K_Flip_Flop j_k_ff_4 (
    .J(\input [6]), .clk(and_1_out), .K(\input [6]), .Q(j_k_ff_4_q), .reset(clr));  // open: Qn, preset
  and _15 (\output [15], j_k_ff_1_q, ADDR, not_1_out);
  and _7 (\output [7], j_k_ff_2_q, ADDR, not_1_out);
  J_K_Flip_Flop j_k_ff_5 (
    .J(\input [13]), .clk(and_1_out), .K(\input [13]), .Q(j_k_ff_5_q), .reset(clr));  // open: Qn, preset
  J_K_Flip_Flop j_k_ff_6 (
    .J(\input [5]), .clk(and_1_out), .K(\input [5]), .Q(j_k_ff_6_q), .reset(clr));  // open: Qn, preset
  and _14 (\output [14], j_k_ff_3_q, ADDR, not_1_out);
  and _6 (\output [6], j_k_ff_4_q, ADDR, not_1_out);
  and _13 (\output [13], j_k_ff_5_q, ADDR, not_1_out);
  and _5 (\output [5], j_k_ff_6_q, ADDR, not_1_out);
  J_K_Flip_Flop j_k_ff_7 (
    .J(\input [12]), .clk(and_1_out), .K(\input [12]), .Q(j_k_ff_7_q), .reset(clr));  // open: Qn, preset
  J_K_Flip_Flop j_k_ff_8 (
    .J(\input [4]), .clk(and_1_out), .K(\input [4]), .Q(j_k_ff_8_q), .reset(clr));  // open: Qn, preset
  J_K_Flip_Flop j_k_ff_9 (
    .J(\input [11]), .clk(and_1_out), .K(\input [11]), .Q(j_k_ff_9_q), .reset(clr));  // open: Qn, preset
  J_K_Flip_Flop j_k_ff_10 (
    .J(\input [3]), .clk(and_1_out), .K(\input [3]), .Q(j_k_ff_10_q), .reset(clr));  // open: Qn, preset
  and _12 (\output [12], j_k_ff_7_q, ADDR, not_1_out);
  and _4 (\output [4], j_k_ff_8_q, ADDR, not_1_out);
  J_K_Flip_Flop j_k_ff_11 (
    .J(\input [10]), .clk(and_1_out), .K(\input [10]), .Q(j_k_ff_11_q), .reset(clr));  // open: Qn, preset
  J_K_Flip_Flop j_k_ff_12 (
    .J(\input [2]), .clk(and_1_out), .K(\input [2]), .Q(j_k_ff_12_q), .reset(clr));  // open: Qn, preset
  and _11 (\output [11], j_k_ff_9_q, ADDR, not_1_out);
  and _3 (\output [3], j_k_ff_10_q, ADDR, not_1_out);
  J_K_Flip_Flop j_k_ff_13 (
    .J(\input [9]), .clk(and_1_out), .K(\input [9]), .Q(j_k_ff_13_q), .reset(clr));  // open: Qn, preset
  J_K_Flip_Flop j_k_ff_14 (
    .J(\input [1]), .clk(and_1_out), .K(\input [1]), .Q(j_k_ff_14_q), .reset(clr));  // open: Qn, preset
  and _10 (\output [10], j_k_ff_11_q, ADDR, not_1_out);
  and _2 (\output [2], j_k_ff_12_q, ADDR, not_1_out);
  J_K_Flip_Flop j_k_ff_15 (
    .J(\input [8]), .clk(and_1_out), .K(\input [8]), .Q(j_k_ff_15_q), .reset(clr));  // open: Qn, preset
  J_K_Flip_Flop j_k_ff_16 (
    .J(\input [0]), .clk(and_1_out), .K(\input [0]), .Q(j_k_ff_16_q), .reset(clr));  // open: Qn, preset
  and _9 (\output [9], j_k_ff_13_q, ADDR, not_1_out);
  and _1 (\output [1], j_k_ff_14_q, ADDR, not_1_out);
  and _8 (\output [8], j_k_ff_15_q, ADDR, not_1_out);
  and _0 (\output [0], j_k_ff_16_q, ADDR, not_1_out);
endmodule

module RAM_8x16__8_1x16 (
  input  CLK,
  input  W_R,
  input  [15:0] \input ,
  input  [2:0] ADDR,
  input  clr,
  output [15:0] \output 
);

  wire _000_out, _001_out, _010_out, _011_out, _100_out, _101_out, _110_out, _111_out, not_1_out, not_2_out,
       not_3_out;
  wire [15:0] ram_1x16_1_output, ram_1x16_2_output, ram_1x16_3_output, ram_1x16_4_output, ram_1x16_5_output,
       ram_1x16_6_output, ram_1x16_7_output, ram_1x16_8_output;

  not not_1 (not_1_out, ADDR[0]);
  not not_2 (not_2_out, ADDR[1]);
  not not_3 (not_3_out, ADDR[2]);
  and _000 (_000_out, not_3_out, not_2_out, not_1_out);
  and _001 (_001_out, not_3_out, not_2_out, ADDR[0]);
  and _010 (_010_out, not_3_out, ADDR[1], not_1_out);
  and _011 (_011_out, not_3_out, ADDR[1], ADDR[0]);
  and _100 (_100_out, ADDR[2], not_2_out, not_1_out);
  and _101 (_101_out, ADDR[2], not_2_out, ADDR[0]);
  and _110 (_110_out, ADDR[2], ADDR[1], not_1_out);
  and _111 (_111_out, ADDR[2], ADDR[1], ADDR[0]);
  RAM_1x16 ram_1x16_1 (
    .CLK(CLK), .R_W(W_R), .ADDR(_000_out), .clr(clr), .\input (\input ), .\output (ram_1x16_1_output));
  RAM_1x16 ram_1x16_2 (
    .CLK(CLK), .R_W(W_R), .ADDR(_001_out), .clr(clr), .\input (\input ), .\output (ram_1x16_2_output));
  RAM_1x16 ram_1x16_3 (
    .CLK(CLK), .R_W(W_R), .ADDR(_010_out), .clr(clr), .\input (\input ), .\output (ram_1x16_3_output));
  RAM_1x16 ram_1x16_4 (
    .CLK(CLK), .R_W(W_R), .ADDR(_011_out), .clr(clr), .\input (\input ), .\output (ram_1x16_4_output));
  RAM_1x16 ram_1x16_5 (
    .CLK(CLK), .R_W(W_R), .ADDR(_100_out), .clr(clr), .\input (\input ), .\output (ram_1x16_5_output));
  RAM_1x16 ram_1x16_6 (
    .CLK(CLK), .R_W(W_R), .ADDR(_101_out), .clr(clr), .\input (\input ), .\output (ram_1x16_6_output));
  RAM_1x16 ram_1x16_7 (
    .CLK(CLK), .R_W(W_R), .ADDR(_110_out), .clr(clr), .\input (\input ), .\output (ram_1x16_7_output));
  RAM_1x16 ram_1x16_8 (
    .CLK(CLK), .R_W(W_R), .ADDR(_111_out), .clr(clr), .\input (\input ), .\output (ram_1x16_8_output));
  Multiplexer #(.select(3), .width(16), .enable("false")) multiplexer_1 (
    .in0(ram_1x16_1_output), .in1(ram_1x16_2_output), .in2(ram_1x16_3_output), .in3(ram_1x16_4_output),
    .in4(ram_1x16_5_output), .in5(ram_1x16_6_output), .in6(ram_1x16_7_output), .in7(ram_1x16_8_output),
    .out(\output ), .sel(ADDR));
endmodule

module _01 (
  input  [3:0] \input ,
  input  R_W,
  input  ADDR,
  input  CLR,
  output [3:0] \output 
);

  wire CLK_out;

  Clock CLK (.out(CLK_out));
  RAM_1x4 RAM_1x4 (.CLK(CLK_out), .R_W(R_W), .ADDR(ADDR), .CLR(CLR), .\input (\input ), .\output (\output ));

  // Notes on the sheet:
  //   // W-write (0)
  //   // R -read  (1)
endmodule

module _02 (
  input  [3:0] \input ,
  input  R_W,
  input  ADDR,
  input  CLR,
  output [3:0] \output 
);

  wire CLK_out;

  Clock CLK (.out(CLK_out));
  RAM_1x4__2_1x2 RAM_1x4 (.CLK(CLK_out), .W_R(R_W), .ADDR(ADDR), .CLR(CLR), .\input (\input ), .\output (\output ));

  // Notes on the sheet:
  //   // W-write (0)
  //   // R -read  (1)
endmodule

module _03 (
  input  [3:0] \input ,
  input  R_W,
  input  ADDR,
  input  CLR,
  output [3:0] \output 
);

  wire CLK_out;

  Clock CLK (.out(CLK_out));
  RAM_2x4__2_1x4 ram_2x4__2_1x4_1 (
    .CLK(CLK_out), .W_R(R_W), .ADDR(ADDR), .CLR(CLR), .\input (\input ), .\output (\output ));

  // Notes on the sheet:
  //   // W-write (0)
  //   // R -read  (1)
  //   RAM 2x4
endmodule

module _04 (
  input  [7:0] \input ,
  input  R_W,
  input  [1:0] ADDR,
  input  CLR,
  output [7:0] \output 
);

  wire CLK_out;

  Clock CLK (.out(CLK_out));
  RAM_4x8__4_2x4 ram_4x8__4_2x4_1 (
    .CLK(CLK_out), .W_R(R_W), .ADDR(ADDR), .CLR(CLR), .\input (\input ), .\output (\output ));

  // Notes on the sheet:
  //   // W-write (0)
  //   // R -read  (1)
  //   RAM 4x8
endmodule

module _05 (
  input  [7:0] \input ,
  input  R_W,
  input  [2:0] ADDR,
  input  CLR,
  output [7:0] \output 
);

  wire CLK_out;

  Clock CLK (.out(CLK_out));
  RAM_8x8__2_4x8 ram_8x8__2_4x8_1 (
    .CLK(CLK_out), .W_R(R_W), .ADDR(ADDR), .CLR(CLR), .\input (\input ), .\output (\output ));

  // Notes on the sheet:
  //   // W-write (0)
  //   // R -read  (1)
  //   RAM 8x8
endmodule

module _06 (
  input  [15:0] \input ,
  input  R_W,
  input  [1:0] ADDR,
  input  CLR,
  output [15:0] \output 
);

  wire CLK_out;

  Clock CLK (.out(CLK_out));
  RAM_4x16__2_4x8 ram_4x16__2_4x8_1 (
    .CLK(CLK_out), .W_R(R_W), .ADDR(ADDR), .CLR(CLR), .\input (\input ), .\output (\output ));

  // Notes on the sheet:
  //   // W-write (0)
  //   // R -read  (1)
  //   RAM 4x16
endmodule

module _07 (
  input  [15:0] \input ,
  input  R_W,
  input  [2:0] ADDR,
  input  CLR,
  output [15:0] \output 
);

  wire CLK_out;

  Clock CLK (.out(CLK_out));
  RAM_8x16__8_1x16 ram_8x16__8_1x16_1 (
    .CLK(CLK_out), .W_R(R_W), .ADDR(ADDR), .clr(CLR), .\input (\input ), .\output (\output ));

  // Notes on the sheet:
  //   // W-write (0)
  //   // R -read  (1)
  //   RAM 8x16
endmodule
