// Logisim project Exemplo_13.circ as structural Verilog
module Down__Asynchronous_counter (
  input  pulse,
  input  _1,
  input  CLR,
  output a,
  output b,
  output c,
  output d
);

  J_K_Flip_Flop j_k_ff_1 (.J(_1), .clk(b), .K(_1), .Qn(a), .reset(CLR));  // open: Q, preset
  J_K_Flip_Flop j_k_ff_2 (.J(_1), .clk(c), .K(_1), .Qn(b), .reset(CLR));  // open: Q, preset
  J_K_Flip_Flop j_k_ff_3 (.J(_1), .clk(d), .K(_1), .Qn(c), .reset(CLR));  // open: Q, preset
  J_K_Flip_Flop j_k_ff_4 (.J(_1), .clk(pulse), .K(_1), .Qn(d), .reset(CLR));  // open: Q, preset
endmodule

module Up__Asynchronous_counter (
  input  pulse,
  input  _1,
  input  CLR,
  output a,
  output b,
  output c,
  output d
);

  wire j_k_ff_2_q, j_k_ff_3_q, j_k_ff_4_q;

  J_K_Flip_Flop j_k_ff_1 (.J(_1), .clk(j_k_ff_2_q), .K(_1), .Qn(a), .reset(CLR));  // open: Q, preset
  J_K_Flip_Flop j_k_ff_2 (.J(_1), .clk(j_k_ff_3_q), .K(_1), .Q(j_k_ff_2_q), .Qn(b), .reset(CLR));  // open: preset
  J_K_Flip_Flop j_k_ff_3 (.J(_1), .clk(j_k_ff_4_q), .K(_1), .Q(j_k_ff_3_q), .Qn(c), .reset(CLR));  // open: preset
  J_K_Flip_Flop j_k_ff_4 (.J(_1), .clk(pulse), .K(_1), .Q(j_k_ff_4_q), .Qn(d), .reset(CLR));  // open: preset
endmodule

module Down__Decade_counter (
  input  pulse,
  input  _1,
  output a,
  output b,
  output c,
  output d
);

  wire and_1_out, j_k_ff_1_qn, j_k_ff_2_qn, j_k_ff_3_qn, j_k_ff_4_qn, not_1_out, not_2_out, not_3_out,
       or_1_out;

  not not_1 (not_1_out, _1);
  and and_1 (and_1_out, not_2_out, j_k_ff_2_qn, not_3_out, j_k_ff_4_qn);
  J_K_Flip_Flop j_k_ff_1 (.J(_1), .clk(pulse), .K(_1), .Q(d), .Qn(j_k_ff_1_qn), .reset(or_1_out));  // open: preset
  or or_1 (or_1_out, not_1_out, and_1_out);
  not not_2 (not_2_out, j_k_ff_1_qn);
  not not_3 (not_3_out, j_k_ff_3_qn);
  J_K_Flip_Flop j_k_ff_2 (.J(_1), .clk(d), .K(_1), .Q(c), .Qn(j_k_ff_2_qn), .reset(or_1_out));  // open: preset
  J_K_Flip_Flop j_k_ff_3 (.J(_1), .clk(c), .K(_1), .Q(b), .Qn(j_k_ff_3_qn), .reset(or_1_out));  // open: preset
  J_K_Flip_Flop j_k_ff_4 (.J(_1), .clk(b), .K(_1), .Q(a), .Qn(j_k_ff_4_qn), .reset(or_1_out));  // open: preset
endmodule

module Up__Decade_counter (
  input  pulse,
  input  _1,
  input  CLR,
  output a,
  output b,
  output c,
  output d
);

  wire j_k_ff_1_qn, j_k_ff_2_qn, j_k_ff_3_qn, nand_1_out, nand_2_out, not_1_out, not_2_out;

  nand nand_1 (nand_1_out, not_1_out, c, not_2_out, a);
  J_K_Flip_Flop j_k_ff_1 (.J(_1), .clk(pulse), .K(_1), .Q(d), .Qn(j_k_ff_1_qn), .reset(nand_2_out));  // open: preset
  nand nand_2 (nand_2_out, CLR, nand_1_out);
  not not_1 (not_1_out, d);
  not not_2 (not_2_out, b);
  J_K_Flip_Flop j_k_ff_2 (
    .J(_1), .clk(j_k_ff_1_qn), .K(_1), .Q(c), .Qn(j_k_ff_2_qn), .reset(nand_2_out));  // open: preset
  J_K_Flip_Flop j_k_ff_3 (
    .J(_1), .clk(j_k_ff_2_qn), .K(_1), .Q(b), .Qn(j_k_ff_3_qn), .reset(nand_2_out));  // open: preset
  J_K_Flip_Flop j_k_ff_4 (.J(_1), .clk(j_k_ff_3_qn), .K(_1), .Q(a), .reset(nand_2_out));  // open: Qn, preset
endmodule

module Down__Synchronous_counter (
  input  CLK,
  input  _1,
  input  CLR,
  output a,
  output b,
  output c,
  output d
);

  wire and_1_out, and_2_out, and_3_out, j_k_ff_1_qn, j_k_ff_2_qn, j_k_ff_3_qn, not_1_out;

  J_K_Flip_Flop j_k_ff_1 (.J(_1), .clk(CLK), .K(_1), .Q(d), .Qn(j_k_ff_1_qn), .reset(CLR));  // open: preset
  and and_1 (and_1_out, j_k_ff_1_qn, not_1_out);
  not not_1 (not_1_out, CLR);
  J_K_Flip_Flop j_k_ff_2 (
    .J(and_1_out), .clk(CLK), .K(and_1_out), .Q(c), .Qn(j_k_ff_2_qn), .reset(CLR));  // open: preset
  and and_2 (and_2_out, j_k_ff_2_qn, and_1_out);
  J_K_Flip_Flop j_k_ff_3 (
    .J(and_2_out), .clk(CLK), .K(and_2_out), .Q(b), .Qn(j_k_ff_3_qn), .reset(CLR));  // open: preset
  J_K_Flip_Flop j_k_ff_4 (.J(and_3_out), .clk(CLK), .K(and_3_out), .Q(a), .reset(CLR));  // open: Qn, preset
  and and_3 (and_3_out, j_k_ff_3_qn, and_2_out);
endmodule

module Up__Synchronous_counter (
  input  CLK,
  input  _1___pulse,
  input  CLR,
  output a,
  output b,
  output c,
  output d
);

  wire and_1_out, and_2_out;

  J_K_Flip_Flop j_k_ff_1 (.J(_1___pulse), .clk(CLK), .K(_1___pulse), .Q(d), .reset(CLR));  // open: Qn, preset
  J_K_Flip_Flop j_k_ff_2 (.J(d), .clk(CLK), .K(d), .Q(c), .reset(CLR));  // open: Qn, preset
  and and_1 (and_1_out, c, d);
  J_K_Flip_Flop j_k_ff_3 (.J(and_1_out), .clk(CLK), .K(and_1_out), .Q(b), .reset(CLR));  // open: Qn, preset
  J_K_Flip_Flop j_k_ff_4 (.J(and_2_out), .clk(CLK), .K(and_2_out), .Q(a), .reset(CLR));  // open: Qn, preset
  and and_2 (and_2_out, b, c, d);
endmodule

module Ring_Counter (
  input  \input ,
  input  clear,
  output a,
  output b,
  output c
);

  wire clock_out, or_1_out;

  Clock clock (.out(clock_out));
  D_Flip_Flop d_ff_1 (.clk(clock_out), .D(or_1_out), .Q(a), .reset(clear));  // open: Qn, preset
  or or_1 (or_1_out, c, \input );
  D_Flip_Flop d_ff_2 (.clk(clock_out), .D(a), .Q(b), .reset(clear));  // open: Qn, preset
  D_Flip_Flop d_ff_3 (.clk(clock_out), .D(b), .Q(c), .reset(clear));  // open: Qn, preset
endmodule

module Twisted_Ring_Counter (
  input  \input ,
  input  clear,
  output a,
  output b,
  output c
);

  wire clock_out, d_ff_3_qn, or_1_out;

  Clock clock (.out(clock_out));
  D_Flip_Flop d_ff_1 (.clk(clock_out), .D(or_1_out), .Q(a), .reset(clear));  // open: Qn, preset
  or or_1 (or_1_out, \input , d_ff_3_qn);
  D_Flip_Flop d_ff_2 (.clk(clock_out), .D(a), .Q(b), .reset(clear));  // open: Qn, preset
  D_Flip_Flop d_ff_3 (.clk(clock_out), .D(b), .Q(c), .Qn(d_ff_3_qn), .reset(clear));  // open: preset
endmodule

module Counter_base_5 (
  input  pulso,
  input  CLR,
  output a,
  output b,
  output c
);

  wire and_1_out, or_1_out, t_ff_2_qn, t_ff_3_qn;

  or or_1 (or_1_out, CLR, and_1_out);
  and and_1 (and_1_out, a, t_ff_2_qn, c);
  T_Flip_Flop t_ff_1 (.clk(t_ff_2_qn), .T(t_ff_2_qn), .Q(a), .reset(or_1_out));  // open: Qn, preset
  T_Flip_Flop t_ff_2 (.clk(t_ff_3_qn), .T(t_ff_3_qn), .Q(b), .Qn(t_ff_2_qn), .reset(or_1_out));  // open: preset
  T_Flip_Flop t_ff_3 (.clk(pulso), .T(pulso), .Q(c), .Qn(t_ff_3_qn), .reset(or_1_out));  // open: preset
endmodule

module _01 (
  input  pulse,
  input  _1,
  input  CLR,
  output a,
  output b,
  output c,
  output d,
  output e,
  output f
);

  J_K_Flip_Flop j_k_ff_1 (.J(_1), .clk(b), .K(_1), .Qn(a), .reset(CLR));  // open: Q, preset
  J_K_Flip_Flop j_k_ff_2 (.J(_1), .clk(c), .K(_1), .Qn(b), .reset(CLR));  // open: Q, preset
  J_K_Flip_Flop j_k_ff_3 (.J(_1), .clk(d), .K(_1), .Qn(c), .reset(CLR));  // open: Q, preset
  J_K_Flip_Flop j_k_ff_4 (.J(_1), .clk(e), .K(_1), .Qn(d), .reset(CLR));  // open: Q, preset
  J_K_Flip_Flop j_k_ff_5 (.J(_1), .clk(f), .K(_1), .Qn(e), .reset(CLR));  // open: Q, preset
  J_K_Flip_Flop j_k_ff_6 (.J(_1), .clk(pulse), .K(_1), .Qn(f), .reset(CLR));  // open: Q, preset
endmodule

module _02 (
  input  pulse,
  input  _1,
  input  CLR,
  output a,
  output b,
  output c,
  output d,
  output e,
  output f
);

  wire j_k_ff_2_q, j_k_ff_3_q, j_k_ff_4_q, j_k_ff_5_q, j_k_ff_6_q;

  J_K_Flip_Flop j_k_ff_1 (.J(_1), .clk(j_k_ff_2_q), .K(_1), .Qn(a), .reset(CLR));  // open: Q, preset
  J_K_Flip_Flop j_k_ff_2 (.J(_1), .clk(j_k_ff_3_q), .K(_1), .Q(j_k_ff_2_q), .Qn(b), .reset(CLR));  // open: preset
  J_K_Flip_Flop j_k_ff_3 (.J(_1), .clk(j_k_ff_4_q), .K(_1), .Q(j_k_ff_3_q), .Qn(c), .reset(CLR));  // open: preset
  J_K_Flip_Flop j_k_ff_4 (.J(_1), .clk(j_k_ff_5_q), .K(_1), .Q(j_k_ff_4_q), .Qn(d), .reset(CLR));  // open: preset
  J_K_Flip_Flop j_k_ff_5 (.J(_1), .clk(j_k_ff_6_q), .K(_1), .Q(j_k_ff_5_q), .Qn(e), .reset(CLR));  // open: preset
  J_K_Flip_Flop j_k_ff_6 (.J(_1), .clk(pulse), .K(_1), .Q(j_k_ff_6_q), .Qn(f), .reset(CLR));  // open: preset
endmodule

module _03 (
  input  pulse,
  input  _1,
  input  CLR,
  output a,
  output b,
  output c,
  output d,
  output e
);

  wire j_k_ff_1_qn, j_k_ff_2_qn, j_k_ff_3_qn, j_k_ff_4_qn, nand_1_out, nand_2_out, not_1_out, not_2_out,
       not_3_out;

  nand nand_1 (nand_1_out, not_1_out, d, not_2_out, b, not_3_out);
  J_K_Flip_Flop j_k_ff_1 (.J(_1), .clk(pulse), .K(_1), .Q(e), .Qn(j_k_ff_1_qn), .reset(nand_2_out));  // open: preset
  nand nand_2 (nand_2_out, CLR, nand_1_out);
  not not_1 (not_1_out, e);
  not not_2 (not_2_out, c);
  not not_3 (not_3_out, a);
  J_K_Flip_Flop j_k_ff_2 (
    .J(_1), .clk(j_k_ff_1_qn), .K(_1), .Q(d), .Qn(j_k_ff_2_qn), .reset(nand_2_out));  // open: preset
  J_K_Flip_Flop j_k_ff_3 (
    .J(_1), .clk(j_k_ff_2_qn), .K(_1), .Q(c), .Qn(j_k_ff_3_qn), .reset(nand_2_out));  // open: preset
  J_K_Flip_Flop j_k_ff_4 (
    .J(_1), .clk(j_k_ff_3_qn), .K(_1), .Q(b), .Qn(j_k_ff_4_qn), .reset(nand_2_out));  // open: preset
  J_K_Flip_Flop j_k_ff_5 (.J(_1), .clk(j_k_ff_4_qn), .K(_1), .Q(a), .reset(nand_2_out));  // open: Qn, preset
endmodule

module _04 (
  input  pulse,
  input  _1,
  output a,
  output b,
  output c,
  output d,
  output e
);

  wire and_1_out, j_k_ff_1_qn, j_k_ff_2_qn, j_k_ff_3_qn, j_k_ff_4_qn, j_k_ff_5_qn, not_1_out, not_2_out,
       not_4_out, or_1_out;

  not not_1 (not_1_out, _1);
  and and_1 (and_1_out, not_2_out, j_k_ff_2_qn, j_k_ff_4_qn, not_4_out);
  J_K_Flip_Flop j_k_ff_1 (.J(_1), .clk(pulse), .K(_1), .Q(e), .Qn(j_k_ff_1_qn), .reset(or_1_out));  // open: preset
  or or_1 (or_1_out, not_1_out, and_1_out);
  not not_2 (not_2_out, j_k_ff_1_qn);
  // NOT_Gate not_3 has open pins: in=j_k_ff_3_qn, out=open
  not not_4 (not_4_out, j_k_ff_5_qn);
  J_K_Flip_Flop j_k_ff_2 (.J(_1), .clk(e), .K(_1), .Q(d), .Qn(j_k_ff_2_qn), .reset(or_1_out));  // open: preset
  J_K_Flip_Flop j_k_ff_3 (.J(_1), .clk(d), .K(_1), .Q(c), .Qn(j_k_ff_3_qn), .reset(or_1_out));  // open: preset
  J_K_Flip_Flop j_k_ff_4 (.J(_1), .clk(c), .K(_1), .Q(b), .Qn(j_k_ff_4_qn), .reset(or_1_out));  // open: preset
  J_K_Flip_Flop j_k_ff_5 (.J(_1), .clk(b), .K(_1), .Q(a), .Qn(j_k_ff_5_qn), .reset(or_1_out));  // open: preset
endmodule

module _05 (
  input  pulso,
  input  CLR,
  output a,
  output b,
  output c
);

  wire and_1_out, or_1_out, t_ff_2_qn, t_ff_3_qn;

  or or_1 (or_1_out, CLR, and_1_out);
  and and_1 (and_1_out, a, b, c);
  T_Flip_Flop t_ff_1 (.clk(t_ff_2_qn), .T(t_ff_2_qn), .Q(a), .reset(or_1_out));  // open: Qn, preset
  T_Flip_Flop t_ff_2 (.clk(t_ff_3_qn), .T(t_ff_3_qn), .Q(b), .Qn(t_ff_2_qn), .reset(or_1_out));  // open: preset
  T_Flip_Flop t_ff_3 (.clk(pulso), .T(pulso), .Q(c), .Qn(t_ff_3_qn), .reset(or_1_out));  // open: preset
endmodule

module _06 (
  input  \input ,
  input  clear,
  output a,
  output b,
  output c,
  output d,
  output e,
  output f
);

  wire clock_out, or_1_out;

  Clock clock (.out(clock_out));
  D_Flip_Flop d_ff_1 (.clk(clock_out), .D(or_1_out), .Q(a), .reset(clear));  // open: Qn, preset
  or or_1 (or_1_out, f, \input );
  D_Flip_Flop d_ff_2 (.clk(clock_out), .D(a), .Q(b), .reset(clear));  // open: Qn, preset
  D_Flip_Flop d_ff_3 (.clk(clock_out), .D(b), .Q(c), .reset(clear));  // open: Qn, preset
  D_Flip_Flop d_ff_4 (.clk(clock_out), .D(c), .Q(d));  // open: Qn, preset, reset
  D_Flip_Flop d_ff_5 (.clk(clock_out), .D(d), .Q(e), .reset(clear));  // open: Qn, preset
  D_Flip_Flop d_ff_6 (.clk(clock_out), .D(e), .Q(f), .reset(clear));  // open: Qn, preset
endmodule

module _07 (
  input  \input ,
  input  clear,
  output a,
  output b,
  output c,
  output d,
  output e,
  output f
);

  wire clock_out, d_ff_6_qn, or_1_out;

  Clock clock (.out(clock_out));
  D_Flip_Flop d_ff_1 (.clk(clock_out), .D(or_1_out), .Q(a), .reset(clear));  // open: Qn, preset
  or or_1 (or_1_out, \input , d_ff_6_qn);
  D_Flip_Flop d_ff_2 (.clk(clock_out), .D(a), .Q(b), .reset(clear));  // open: Qn, preset
  D_Flip_Flop d_ff_3 (.clk(clock_out), .D(b), .Q(c), .reset(clear));  // open: Qn, preset
  D_Flip_Flop d_ff_4 (.clk(clock_out), .D(c), .Q(d), .reset(clear));  // open: Qn, preset
  D_Flip_Flop d_ff_5 (.clk(clock_out), .D(d), .Q(e), .reset(clear));  // open: Qn, preset
  D_Flip_Flop d_ff_6 (.clk(clock_out), .D(e), .Q(f), .Qn(d_ff_6_qn), .reset(clear));  // open: preset
endmodule
