// Logisim project Exemplo_14.circ as structural Verilog
module Flip_flops (
  input  in_1,
  input  in_2,
  input  in_3,
  input  in_4,
  input  in_5,
  input  in_6,
  input  in_7,
  input  in_8,
  input  in_9,
  input  in_10,
  output out_11,
  output out_12,
  output out_13,
  output out_14,
  output out_15,
  output out_16,
  output out_17,
  output out_18
);

  wire clock_1_out, clock_2_out, clock_3_out, clock_4_out;

  Clock clock_1 (.out(clock_1_out));
  Clock clock_2 (.out(clock_2_out));
  S_R_Flip_Flop s_r_ff_1 (
    .S(in_1), .clk(clock_1_out), .R(in_3), .Q(out_11), .Qn(out_13), .reset(in_5));  // open: preset
  D_Flip_Flop d_ff_1 (.clk(clock_2_out), .D(in_7), .Q(out_15), .Qn(out_17), .reset(in_9));  // open: preset
  Clock clock_3 (.out(clock_3_out));
  Clock clock_4 (.out(clock_4_out));
  J_K_Flip_Flop j_k_ff_1 (
    .J(in_2), .clk(clock_3_out), .K(in_4), .Q(out_12), .Qn(out_14), .reset(in_6));  // open: preset
  T_Flip_Flop t_ff_1 (.clk(clock_4_out), .T(in_8), .Q(out_16), .Qn(out_18), .reset(in_10));  // open: preset

  // Notes on the sheet:
  //   Q      = S + R'.Q
  //   t+1                         t  
  //     Q      = D
  //               t+1                           
  //   Flip-flops
  //   Q      = J.Q' + K'.Q
  //   Q      = T xor Q
  //   t+1             t                t  
  //   t+1                        t  
endmodule

module Parallel_In_Serial_Out (
  input  LD,
  input  d0,
  input  d1,
  input  d2,
  input  d3,
  input  clk,
  input  clr,
  output a,
  output b,
  output c,
  output d
);

  wire and_1_out, and_2_out, and_3_out, and_4_out;

  and and_1 (and_1_out, LD, d3);
  D_Flip_Flop d_ff_1 (.clk(clk), .D(1'b0), .Q(a), .preset(and_1_out), .reset(clr));  // open: Qn
  and and_2 (and_2_out, LD, d2);
  D_Flip_Flop d_ff_2 (.clk(clk), .D(a), .Q(b), .preset(and_2_out), .reset(clr));  // open: Qn
  and and_3 (and_3_out, LD, d1);
  D_Flip_Flop d_ff_3 (.clk(clk), .D(b), .Q(c), .preset(and_3_out), .reset(clr));  // open: Qn
  and and_4 (and_4_out, LD, d0);
  D_Flip_Flop d_ff_4 (.clk(clk), .D(c), .Q(d), .preset(and_4_out), .reset(clr));  // open: Qn

  // Notes on the sheet:
  //   Parallel_In/Serial_Out
endmodule

module Semaphore (
  input  clk,
  input  clr,
  input  pulse
);

  wire and_1_out, j_k_ff_1_q, j_k_ff_1_qn, j_k_ff_2_q, j_k_ff_2_qn, j_k_ff_3_q, not_1_out, or_1_out;

  not not_1 (not_1_out, or_1_out);
  or or_1 (or_1_out, pulse, and_1_out);
  and and_1 (and_1_out, j_k_ff_1_qn, j_k_ff_2_qn, j_k_ff_3_q);
  LED GREEN (.in(j_k_ff_1_q));
  J_K_Flip_Flop j_k_ff_1 (
    .J(or_1_out), .clk(clk), .K(not_1_out), .Q(j_k_ff_1_q), .Qn(j_k_ff_1_qn), .reset(clr));  // open: preset
  LED YELLOW (.in(j_k_ff_2_q));
  J_K_Flip_Flop j_k_ff_2 (
    .J(j_k_ff_1_q), .clk(clk), .K(j_k_ff_1_qn), .Q(j_k_ff_2_q), .Qn(j_k_ff_2_qn), .reset(clr));  // open: preset
  LED RED (.in(j_k_ff_3_q));
  J_K_Flip_Flop j_k_ff_3 (.J(j_k_ff_2_q), .clk(clk), .K(j_k_ff_2_qn), .Q(j_k_ff_3_q), .reset(clr));  // open: Qn, preset

  // Notes on the sheet:
  //   Semaphore
endmodule

module Ring_Counter (
  input  \input ,
  input  clear,
  output a,
  output b,
  output c
);

  wire clock_out, or_1_out;

  Clock clock (.out(clock_out));
  D_Flip_Flop d_ff_1 (.clk(clock_out), .D(or_1_out), .Q(a), .reset(clear));  // open: Qn, preset
  or or_1 (or_1_out, c, \input );
  D_Flip_Flop d_ff_2 (.clk(clock_out), .D(a), .Q(b), .reset(clear));  // open: Qn, preset
  D_Flip_Flop d_ff_3 (.clk(clock_out), .D(b), .Q(c), .reset(clear));  // open: Qn, preset

  // Notes on the sheet:
  //   Ring Counter
endmodule

module Twisted_Ring_Counter (
  input  \input ,
  input  clear,
  output a,
  output b,
  output c
);

  wire clock_out, d_ff_3_qn, or_1_out;

  Clock clock (.out(clock_out));
  D_Flip_Flop d_ff_1 (.clk(clock_out), .D(or_1_out), .Q(a), .reset(clear));  // open: Qn, preset
  or or_1 (or_1_out, \input , d_ff_3_qn);
  D_Flip_Flop d_ff_2 (.clk(clock_out), .D(a), .Q(b), .reset(clear));  // open: Qn, preset
  D_Flip_Flop d_ff_3 (.clk(clock_out), .D(b), .Q(c), .Qn(d_ff_3_qn), .reset(clear));  // open: preset

  // Notes on the sheet:
  //   Twister Ring Counter
endmodule

module Left__Shift_Register__D (
  input  clk,
  input  data,
  input  clr,
  output a,
  output b,
  output c,
  output d
);

  D_Flip_Flop d_ff_1 (.clk(clk), .D(b), .Q(a), .reset(clr));  // open: Qn, preset
  D_Flip_Flop d_ff_2 (.clk(clk), .D(c), .Q(b), .reset(clr));  // open: Qn, preset
  D_Flip_Flop d_ff_3 (.clk(clk), .D(d), .Q(c), .reset(clr));  // open: Qn, preset
  D_Flip_Flop d_ff_4 (.clk(clk), .D(data), .Q(d), .reset(clr));  // open: Qn, preset

  // Notes on the sheet:
  //   (Left) Shift Register (D)
endmodule

module Right__Shift_Register__D (
  input  clk,
  input  data,
  input  clr,
  output a,
  output b,
  output c,
  output d
);

  D_Flip_Flop d_ff_1 (.clk(clk), .D(data), .Q(a), .reset(clr));  // open: Qn, preset
  D_Flip_Flop d_ff_2 (.clk(clk), .D(a), .Q(b), .reset(clr));  // open: Qn, preset
  D_Flip_Flop d_ff_3 (.clk(clk), .D(b), .Q(c), .reset(clr));  // open: Qn, preset
  D_Flip_Flop d_ff_4 (.clk(clk), .D(c), .Q(d), .reset(clr));  // open: Qn, preset

  // Notes on the sheet:
  //   (Right) Shift Register (D)
endmodule

module Left__Rotate_Register__D (
  input  clk,
  input  data,
  input  clr,
  output a,
  output b,
  output c
);

  wire or_1_out;

  or or_1 (or_1_out, a, data);
  D_Flip_Flop d_ff_1 (.clk(clk), .D(b), .Q(a), .reset(clr));  // open: Qn, preset
  D_Flip_Flop d_ff_2 (.clk(clk), .D(c), .Q(b), .reset(clr));  // open: Qn, preset
  D_Flip_Flop d_ff_3 (.clk(clk), .D(or_1_out), .Q(c), .reset(clr));  // open: Qn, preset

  // Notes on the sheet:
  //   (Left) Rotate Register (D)
endmodule

module Right__Rotate_Register__D (
  input  clk,
  input  data,
  input  clr,
  output a,
  output b,
  output c
);

  wire or_1_out;

  or or_1 (or_1_out, c, data);
  D_Flip_Flop d_ff_1 (.clk(clk), .D(or_1_out), .Q(a), .reset(clr));  // open: Qn, preset
  D_Flip_Flop d_ff_2 (.clk(clk), .D(a), .Q(b), .reset(clr));  // open: Qn, preset
  D_Flip_Flop d_ff_3 (.clk(clk), .D(b), .Q(c), .reset(clr));  // open: Qn, preset

  // Notes on the sheet:
  //   (Right) Rotate Register (D)
endmodule

module _01 (
  input  LD,
  input  clk,
  input  data,
  input  clr,
  output a,
  output b,
  output c,
  output d,
  output e,
  output f
);

  D_Flip_Flop d_ff_1 (.clk(clk), .D(b), .Q(a), .reset(clr));  // open: Qn, preset
  D_Flip_Flop d_ff_2 (.clk(clk), .D(c), .Q(b), .reset(clr));  // open: Qn, preset
  D_Flip_Flop d_ff_3 (.clk(clk), .D(d), .Q(c), .reset(clr));  // open: Qn, preset
  D_Flip_Flop d_ff_4 (.clk(clk), .D(e), .Q(d), .reset(clr));  // open: Qn, preset
  D_Flip_Flop d_ff_5 (.clk(clk), .D(f), .Q(e), .reset(clr));  // open: Qn, preset
  D_Flip_Flop d_ff_6 (.clk(clk), .D(data), .Q(f), .preset(LD), .reset(clr));  // open: Qn
endmodule

module _02 (
  input  LD,
  input  clk,
  input  data,
  input  clr,
  output a,
  output b,
  output c,
  output d,
  output e,
  output f
);

  D_Flip_Flop d_ff_1 (.clk(clk), .D(b), .Q(a), .preset(LD), .reset(clr));  // open: Qn
  D_Flip_Flop d_ff_2 (.clk(clk), .D(c), .Q(b), .preset(LD), .reset(clr));  // open: Qn
  D_Flip_Flop d_ff_3 (.clk(clk), .D(d), .Q(c), .preset(LD), .reset(clr));  // open: Qn
  D_Flip_Flop d_ff_4 (.clk(clk), .D(e), .Q(d), .preset(LD), .reset(clr));  // open: Qn
  D_Flip_Flop d_ff_5 (.clk(clk), .D(f), .Q(e), .preset(LD), .reset(clr));  // open: Qn
  D_Flip_Flop d_ff_6 (.clk(clk), .D(data), .Q(f), .preset(LD), .reset(clr));  // open: Qn
endmodule

module _03 (
  input  LD,
  input  clk,
  input  data,
  input  clr,
  output a,
  output b,
  output c,
  output d,
  output e,
  output f
);

  wire or_1_out;

  or or_1 (or_1_out, f, data);
  D_Flip_Flop d_ff_1 (.clk(clk), .D(or_1_out), .Q(a), .reset(clr));  // open: Qn, preset
  D_Flip_Flop d_ff_2 (.clk(clk), .D(a), .Q(b), .reset(clr));  // open: Qn, preset
  D_Flip_Flop d_ff_3 (.clk(clk), .D(b), .Q(c), .reset(clr));  // open: Qn, preset
  D_Flip_Flop d_ff_4 (.clk(clk), .D(c), .Q(d), .reset(clr));  // open: Qn, preset
  D_Flip_Flop d_ff_5 (.clk(clk), .D(d), .Q(e), .reset(clr));  // open: Qn, preset
  D_Flip_Flop d_ff_6 (.clk(clk), .D(e), .Q(f), .preset(LD), .reset(clr));  // open: Qn
endmodule

module _04 (
  input  LD,
  input  clk,
  input  data,
  input  clr,
  output a,
  output b,
  output c,
  output d,
  output e,
  output f
);

  wire d_ff_1_qn, or_1_out;

  or or_1 (or_1_out, data, d_ff_1_qn);
  D_Flip_Flop d_ff_1 (.clk(clk), .D(b), .Q(a), .Qn(d_ff_1_qn), .reset(clr));  // open: preset
  D_Flip_Flop d_ff_2 (.clk(clk), .D(c), .Q(b), .reset(clr));  // open: Qn, preset
  D_Flip_Flop d_ff_3 (.clk(clk), .D(d), .Q(c), .reset(clr));  // open: Qn, preset
  D_Flip_Flop d_ff_4 (.clk(clk), .D(e), .Q(d), .reset(clr));  // open: Qn, preset
  D_Flip_Flop d_ff_5 (.clk(clk), .D(f), .Q(e), .reset(clr));  // open: Qn, preset
  D_Flip_Flop d_ff_6 (.clk(clk), .D(or_1_out), .Q(f), .preset(LD), .reset(clr));  // open: Qn
endmodule

module _05 (
  input  LD,
  input  d0,
  input  d1,
  input  d2,
  input  d3,
  input  d4,
  input  d5,
  input  clk,
  input  clr,
  output a,
  output b,
  output c,
  output d,
  output e,
  output f
);

  wire and_1_out, and_2_out, and_3_out, and_4_out, and_5_out, and_6_out;

  and and_1 (and_1_out, LD, d5);
  D_Flip_Flop d_ff_1 (.clk(clk), .D(1'b0), .Q(a), .preset(and_1_out), .reset(clr));  // open: Qn
  and and_2 (and_2_out, LD, d4);
  D_Flip_Flop d_ff_2 (.clk(clk), .D(a), .Q(b), .preset(and_2_out), .reset(clr));  // open: Qn
  and and_3 (and_3_out, LD, d3);
  D_Flip_Flop d_ff_3 (.clk(clk), .D(b), .Q(c), .preset(and_3_out), .reset(clr));  // open: Qn
  and and_4 (and_4_out, LD, d2);
  and and_5 (and_5_out, d1, LD);
  D_Flip_Flop d_ff_4 (.clk(clk), .D(c), .Q(d), .preset(and_4_out), .reset(clr));  // open: Qn
  D_Flip_Flop d_ff_5 (.clk(clk), .D(d), .Q(e), .preset(and_5_out), .reset(clr));  // open: Qn
  and and_6 (and_6_out, d0, LD);
  D_Flip_Flop d_ff_6 (.clk(clk), .D(e), .Q(f), .preset(and_6_out), .reset(clr));  // open: Qn
endmodule

module _06 (
  input  LD,
  input  clk,
  input  data,
  input  clr,
  output a,
  output b,
  output c,
  output d,
  output e
);

  wire or_1_out;

  or or_1 (or_1_out, a, data);
  D_Flip_Flop d_ff_1 (.clk(clk), .D(b), .Q(a), .preset(LD), .reset(clr));  // open: Qn
  D_Flip_Flop d_ff_2 (.clk(clk), .D(c), .Q(b), .preset(LD), .reset(clr));  // open: Qn
  D_Flip_Flop d_ff_3 (.clk(clk), .D(d), .Q(c), .preset(LD), .reset(clr));  // open: Qn
  D_Flip_Flop d_ff_4 (.clk(clk), .D(e), .Q(d), .preset(LD), .reset(clr));  // open: Qn
  D_Flip_Flop d_ff_5 (.clk(clk), .D(or_1_out), .Q(e), .preset(LD), .reset(clr));  // open: Qn

  // Notes on the sheet:
  //   // ao realizar preset em todos os estagios, nao esta' sendo possivel novas entradas de dados.
endmodule

module _07 (
  input  LD,
  input  clk,
  input  data,
  input  clr,
  output a,
  output b,
  output c,
  output d,
  output e
);

  wire d_ff_5_qn, or_1_out;

  or or_1 (or_1_out, data, d_ff_5_qn);
  D_Flip_Flop d_ff_1 (.clk(clk), .D(or_1_out), .Q(a), .preset(LD), .reset(clr));  // open: Qn
  D_Flip_Flop d_ff_2 (.clk(clk), .D(a), .Q(b), .preset(LD), .reset(clr));  // open: Qn
  D_Flip_Flop d_ff_3 (.clk(clk), .D(b), .Q(c), .preset(LD), .reset(clr));  // open: Qn
  D_Flip_Flop d_ff_4 (.clk(clk), .D(c), .Q(d), .preset(LD), .reset(clr));  // open: Qn
  D_Flip_Flop d_ff_5 (.clk(clk), .D(d), .Q(e), .Qn(d_ff_5_qn), .preset(LD), .reset(clr));
endmodule
