// Logisim project Exemplo_17.circ as structural Verilog
module tipo_D (
  input  clk,
  input  c,
  input  clr,
  output [1:0] Q
);

  wire and_1_out, and_2_out, and_3_out, and_4_out, not_1_out, not_2_out, not_3_out, or_1_out, or_2_out;

  not not_1 (not_1_out, c);
  not not_2 (not_2_out, c);
  not not_3 (not_3_out, Q[1]);
  and and_1 (and_1_out, Q[1], not_1_out);
  or or_1 (or_1_out, and_1_out, and_2_out);
  and and_2 (and_2_out, Q[0], c);
  and and_3 (and_3_out, Q[0], not_2_out);
  or or_2 (or_2_out, and_3_out, and_4_out);
  and and_4 (and_4_out, not_3_out, c);
  D_Flip_Flop Da (.clk(clk), .D(or_1_out), .Q(Q[1]), .reset(clr));  // open: Qn, preset
  D_Flip_Flop Db (.clk(clk), .D(or_2_out), .Q(Q[0]), .reset(clr));  // open: Qn, preset
endmodule

module tipo_T (
  input  clk,
  input  c,
  input  clr,
  output [1:0] Q
);

  wire and_1_out, and_2_out, and_3_out, and_4_out, not_1_out, not_2_out, not_3_out, not_4_out, or_1_out,
       or_2_out;

  not not_1 (not_1_out, Q[1]);
  not not_2 (not_2_out, Q[0]);
  not not_3 (not_3_out, Q[1]);
  not not_4 (not_4_out, Q[0]);
  and and_1 (and_1_out, not_1_out, Q[0], c);
  or or_1 (or_1_out, and_1_out, and_2_out);
  and and_2 (and_2_out, Q[1], not_2_out, c);
  and and_3 (and_3_out, not_3_out, not_4_out, c);
  or or_2 (or_2_out, and_3_out, and_4_out);
  and and_4 (and_4_out, Q[1], Q[0], c);
  T_Flip_Flop Ta (.clk(clk), .T(or_1_out), .Q(Q[1]), .reset(clr));  // open: Qn, preset
  T_Flip_Flop Tb (.clk(clk), .T(or_2_out), .Q(Q[0]), .reset(clr));  // open: Qn, preset
endmodule

module tipo_JK_modoSR (
  input  clk,
  input  c,
  input  clr,
  output [1:0] Q
);

  wire and_1_out, and_2_out, and_3_out, and_4_out, not_1_out, not_2_out, not_3_out, not_4_out;

  not not_1 (not_1_out, Q[1]);
  not not_2 (not_2_out, Q[0]);
  not not_3 (not_3_out, Q[1]);
  not not_4 (not_4_out, Q[0]);
  and and_1 (and_1_out, not_1_out, Q[0], c);
  and and_2 (and_2_out, Q[1], not_2_out, c);
  and and_3 (and_3_out, not_3_out, not_4_out, c);
  and and_4 (and_4_out, Q[1], Q[0], c);
  J_K_Flip_Flop JaKa (.J(and_1_out), .clk(clk), .K(and_2_out), .Q(Q[1]), .reset(clr));  // open: Qn, preset
  J_K_Flip_Flop JbKb (.J(and_3_out), .clk(clk), .K(and_4_out), .Q(Q[0]), .reset(clr));  // open: Qn, preset
endmodule

module tipo_JK_modoToogle (
  input  clk,
  input  c,
  input  clr,
  output [1:0] Q
);

  wire and_1_out, and_2_out, and_3_out, and_4_out, and_5_out, and_6_out, and_7_out, and_8_out, not_1_out,
       not_2_out, not_3_out, not_4_out, not_5_out, not_6_out, not_7_out, not_8_out, or_1_out, or_2_out,
       or_3_out, or_4_out;

  not not_1 (not_1_out, Q[1]);
  not not_2 (not_2_out, Q[0]);
  not not_3 (not_3_out, Q[1]);
  not not_4 (not_4_out, Q[0]);
  not not_5 (not_5_out, Q[1]);
  not not_6 (not_6_out, Q[0]);
  not not_7 (not_7_out, Q[0]);
  not not_8 (not_8_out, c);
  and and_1 (and_1_out, not_1_out, Q[0], c);
  or or_1 (or_1_out, and_1_out, and_2_out);
  and and_2 (and_2_out, Q[1], not_2_out, c);
  and and_3 (and_3_out, not_3_out, Q[0], c);
  or or_2 (or_2_out, and_3_out, and_4_out);
  and and_4 (and_4_out, Q[1], not_4_out, c);
  and and_5 (and_5_out, not_5_out, not_6_out, c);
  or or_3 (or_3_out, and_5_out, and_6_out);
  and and_6 (and_6_out, Q[1], Q[0], c);
  and and_7 (and_7_out, Q[1], not_7_out, not_8_out);
  or or_4 (or_4_out, and_7_out, and_8_out);
  and and_8 (and_8_out, Q[1], Q[0], c);
  J_K_Flip_Flop JaKa (.J(or_1_out), .clk(clk), .K(or_2_out), .Q(Q[1]), .reset(clr));  // open: Qn, preset
  J_K_Flip_Flop JbKb (.J(or_3_out), .clk(clk), .K(or_4_out), .Q(Q[0]), .reset(clr));  // open: Qn, preset
endmodule

module tipo_SR (
  input  clk,
  input  c,
  input  clr,
  output [1:0] Q
);

  wire and_1_out, and_2_out, and_3_out, and_4_out, not_1_out, not_2_out, not_3_out, not_4_out;

  not not_1 (not_1_out, Q[1]);
  not not_2 (not_2_out, Q[0]);
  not not_3 (not_3_out, Q[1]);
  not not_4 (not_4_out, Q[0]);
  and and_1 (and_1_out, not_1_out, Q[0], c);
  and and_2 (and_2_out, Q[1], not_2_out, c);
  and and_3 (and_3_out, not_3_out, not_4_out, c);
  and and_4 (and_4_out, Q[1], Q[0], c);
  S_R_Flip_Flop SaRa (.S(and_1_out), .clk(clk), .R(and_2_out), .Q(Q[1]), .reset(clr));  // open: Qn, preset
  S_R_Flip_Flop SbRb (.S(and_3_out), .clk(clk), .R(and_4_out), .Q(Q[0]), .reset(clr));  // open: Qn, preset
endmodule

module _01 (
  input  \input ,
  input  clr,
  output [1:0] Q_atual
);

  wire clk_out;

  Clock clk (.out(clk_out));
  tipo_D tipo_d_1 (.clk(clk_out), .c(\input ), .clr(clr), .Q(Q_atual));
endmodule

module _02 (
  input  \input ,
  input  clr,
  output [1:0] Q_atual
);

  wire clk_out;

  Clock clk (.out(clk_out));
  tipo_JK_modoSR tipo_jk_modosr_1 (.clk(clk_out), .c(\input ), .clr(clr), .Q(Q_atual));
endmodule

module _03 (
  input  \input ,
  input  clr,
  output [1:0] Q_atual
);

  wire clk_out;

  Clock clk (.out(clk_out));
  tipo_JK_modoToogle tipo_jk_modotoogle_1 (.clk(clk_out), .c(\input ), .clr(clr), .Q(Q_atual));
endmodule

module _04 (
  input  clk,
  input  clr
);

  wire t_ff_1_q, t_ff_2_q;

  T_Flip_Flop t_ff_1 (.clk(clk), .T(1'b1), .Q(t_ff_1_q), .reset(clr));  // open: Qn, preset
  T_Flip_Flop t_ff_2 (.clk(t_ff_1_q), .T(1'b1), .Q(t_ff_2_q), .reset(clr));  // open: Qn, preset
  T_Flip_Flop t_ff_3 (.clk(t_ff_2_q), .T(1'b1), .reset(clr));  // open: Q, Qn, preset
endmodule

module _05 (
  input  clk,
  input  clr
);

  wire t_ff_1_qn, t_ff_2_qn;

  T_Flip_Flop t_ff_1 (.clk(clk), .T(1'b1), .Qn(t_ff_1_qn), .reset(clr));  // open: Q, preset
  T_Flip_Flop t_ff_2 (.clk(t_ff_1_qn), .T(1'b1), .Qn(t_ff_2_qn), .reset(clr));  // open: Q, preset
  T_Flip_Flop t_ff_3 (.clk(t_ff_2_qn), .T(1'b1), .reset(clr));  // open: Q, Qn, preset
endmodule
