// Logisim project Recuperacao_01.circ as structural Verilog: 10 circuits, main circuit 01a
module _01a (
  input  a,
  input  b,
  input  c,
  input  d,
  output s
);

  wire _0_out, _1_out, _5_out, _6_out, _8_out, _9_out, C_out, E_out, not_1_out, not_2_out, not_3_out,
       not_4_out;

  not not_1 (not_1_out, a);
  not not_2 (not_2_out, b);
  not not_3 (not_3_out, c);
  not not_4 (not_4_out, d);
  and _0 (_0_out, not_1_out, not_2_out, not_3_out, not_4_out);
  and _1 (_1_out, not_1_out, not_2_out, not_3_out, d);
  and _5 (_5_out, not_1_out, b, not_3_out, d);
  and _6 (_6_out, not_1_out, b, c, not_4_out);
  and _8 (_8_out, a, not_2_out, not_3_out, not_4_out);
  and _9 (_9_out, a, not_2_out, not_3_out, d);
  and u_C (C_out, a, b, not_3_out, not_4_out);
  and E (E_out, a, b, c, not_4_out);
  or or_1 (s, _0_out, _1_out, _5_out, _6_out, _8_out, _9_out, C_out, E_out);

  // Notes on the sheet:
  //   SoP (0,1,5,6,8,9,C,E)
endmodule

module _01b (
  input  A,
  input  B,
  input  C,
  input  D,
  output S
);

  wire _2_out, _3_out, _4_out, _7_out, A_out, B_out, D_out, F_out, not_1_out, not_2_out, not_3_out, not_4_out;

  not not_1 (not_1_out, A);
  not not_2 (not_2_out, C);
  not not_3 (not_3_out, B);
  not not_4 (not_4_out, D);
  or _2 (_2_out, A, B, not_2_out, D);
  or _3 (_3_out, A, B, not_2_out, not_4_out);
  or _4 (_4_out, A, not_3_out, C, D);
  or _7 (_7_out, A, not_3_out, not_2_out, not_4_out);
  or u_A (A_out, not_1_out, B, not_2_out, D);
  or u_B (B_out, not_1_out, B, not_2_out, not_4_out);
  or u_D (D_out, not_1_out, not_3_out, C, not_4_out);
  or F (F_out, not_1_out, not_3_out, not_2_out, not_4_out);
  and and_1 (S, _2_out, _3_out, _4_out, _7_out, A_out, B_out, D_out, F_out);

  // Notes on the sheet:
  //   PoS (2,3,4,7,A,B,D,F)
endmodule

module _01c (
  input  a,
  input  b,
  input  c,
  input  d,
  output s
);

  wire _5_out, _6_out, and_1_out, and_2_out, not_1_out, not_2_out, not_3_out, not_4_out;

  not not_1 (not_1_out, a);
  not not_2 (not_2_out, c);
  not not_3 (not_3_out, b);
  not not_4 (not_4_out, d);
  and and_1 (and_1_out, not_3_out, not_2_out);
  and and_2 (and_2_out, b, c, not_4_out);
  and _5 (_5_out, not_1_out, not_2_out, d);
  and _6 (_6_out, a, not_2_out, not_4_out);
  or or_1 (s, and_1_out, and_2_out, _5_out, _6_out);

  // Notes on the sheet:
  //   SoP (0,1,5,6,8,9,C,E)
  //   b' . c'
  //   b . c . d'
  //   a' . c' . d
  //   a . c' . d'
endmodule

module _01d (
  input  A,
  input  B,
  input  C,
  input  D,
  output s
);

  wire not_1_out, not_2_out, not_3_out, not_4_out, or_1_out, or_2_out, or_3_out, or_4_out;

  not not_1 (not_1_out, A);
  not not_2 (not_2_out, C);
  not not_3 (not_3_out, B);
  not not_4 (not_4_out, D);
  or or_1 (or_1_out, not_2_out, not_4_out);
  or or_2 (or_2_out, B, not_2_out);
  or or_3 (or_3_out, not_1_out, not_3_out, not_4_out);
  or or_4 (or_4_out, A, not_3_out, C, D);
  and and_1 (s, or_1_out, or_2_out, or_3_out, or_4_out);

  // Notes on the sheet:
  //   PoS(2,3,4,7,A,B,D,F)
  //   C' + D'
  //   B + C'
  //   A' + B' + D'
  //   A + B' + C + D
endmodule

module _02 (
  input  a,
  input  b,
  input  c,
  output s
);

  wire and_1_out, not_1_out;

  not not_1 (not_1_out, c);
  and and_1 (and_1_out, b, not_1_out);
  or u_s (s, a, and_1_out);

  // Notes on the sheet:
  //   f (a,b,c)
  //   w2
  //   w1
endmodule

module _03 (
  input  a,
  input  b,
  input  c,
  output s
);

  wire and_1_out, and_2_out, not_1_out, not_2_out, not_3_out, or_1_out;

  not not_1 (not_1_out, a);
  or or_1 (or_1_out, not_1_out, not_2_out);
  not not_2 (not_2_out, b);
  not not_3 (not_3_out, and_1_out);
  and and_1 (and_1_out, a, c);
  and and_2 (and_2_out, or_1_out, not_3_out);
  not not_4 (s, and_2_out);

  // Notes on the sheet:
  //   A0113 (a,b,c)
endmodule

module _03_simple (
  input  a,
  input  b,
  input  c,
  output s
);

  wire and_1_out, and_2_out;

  and and_1 (and_1_out, a, b);
  and and_2 (and_2_out, a, c);
  or or_1 (s, and_1_out, and_2_out);

  // Notes on the sheet:
  //   A0113_simple (a,b,c)
endmodule

module _04a (
  input  a,
  input  b,
  input  c,
  output s
);

  wire w1_out, w2_out, w3_out, w4_out, w5_out;

  nor w1 (w1_out, a, a);
  nor w2 (w2_out, a, a);
  nor w3 (w3_out, w1_out, b);
  nor w4 (w4_out, w2_out, b);
  nor w5 (w5_out, w3_out, w4_out);
  nor u_s (s, w5_out, c);
endmodule

module _04b (
  input  a,
  input  b,
  output s,
  output s_2
);

  wire w1_out, w2_out, w3_out, w4_out;

  nand w1 (w1_out, a, a);
  nand w2 (w2_out, b, b);
  nand w4 (w4_out, a, w2_out);
  nand w3 (w3_out, w1_out, b);
  nand u_s (s, w4_out, w3_out);
  xor a_b (s_2, a, b);
endmodule

module _04c (
  input  a,
  input  b,
  input  c,
  output s
);

  wire multiplexer_1_out, multiplexer_2_out, not_1_out, not_2_out;

  not not_1 (not_1_out, a);
  Multiplexer #(.enable("false")) multiplexer_1 (.in0(b), .in1(c), .out(multiplexer_1_out), .sel(a));
  Multiplexer #(.enable("false")) multiplexer_2 (.in0(not_1_out), .in1(b), .out(multiplexer_2_out), .sel(c));
  not not_2 (not_2_out, c);
  Multiplexer #(.enable("false")) multiplexer_3 (
    .in0(multiplexer_1_out), .in1(multiplexer_2_out), .out(s), .sel(not_2_out));
endmodule
